// Logisim project FullSub.circ as structural Verilog: 1 circuit, main circuit main
module main (
  input  a,
  input  b,
  input  c_in,
  output sub,
  output borrow
);

  wire and_1_out, and_2_out, not_1_out, not_2_out, xor_1_out;

  not not_1 (not_1_out, a);
  xor xor_1 (xor_1_out, a, b);
  and and_1 (and_1_out, not_1_out, b);
  not not_2 (not_2_out, xor_1_out);
  xor xor_2 (sub, xor_1_out, c_in);
  and and_2 (and_2_out, not_2_out, c_in);
  or or_1 (borrow, and_1_out, and_2_out);
endmodule
