// Logisim project Full_Sub.circ as structural Verilog: 1 circuit, main circuit main
module main (
  input  A,
  input  B,
  input  Bin,
  output out_4
);

  wire and_1_out, and_2_out, not_1_out, xnor_1_out, xor_1_out;

  not not_1 (not_1_out, A);
  // OR_Gate or_1 has open pins: in0=Bin, in1=B, out=open
  xnor xnor_1 (xnor_1_out, B, Bin);
  xor xor_1 (xor_1_out, Bin, B);
  and and_1 (and_1_out, A, xnor_1_out);
  and and_2 (and_2_out, not_1_out, xor_1_out);
  or or_2 (out_4, and_1_out, and_2_out);
endmodule
