// Logisim project 1.circ as structural Verilog: 1 circuit, main circuit main
module main (
  input  Co,
  input  A,
  input  B,
  input  C,
  input  D,
  output S1,
  output S2,
  output out_8
);

  wire and_1_out, and_2_out, and_3_out, and_4_out, or_1_out, xor_1_out, xor_2_out;

  xor xor_1 (xor_1_out, A, B);
  xor xor_2 (xor_2_out, C, D);
  xor xor_3 (S1, Co, xor_1_out);
  and and_1 (and_1_out, Co, xor_1_out);
  and and_2 (and_2_out, B, A);
  or or_1 (or_1_out, and_1_out, and_2_out);
  xor xor_4 (S2, or_1_out, xor_2_out);
  and and_3 (and_3_out, or_1_out, xor_2_out);
  and and_4 (and_4_out, D, C);
  or or_2 (out_8, and_3_out, and_4_out);

  // Notes on the sheet:
  //   CARRY
endmodule
