// Logisim project 2-bit_Sub.circ as structural Verilog: 1 circuit, main circuit main
module main (
  input  Bin,
  input  a1,
  input  a0,
  input  b1,
  input  b0,
  output Borrow,
  output out_7,
  output out_8
);

  wire and_1_out, and_2_out, and_3_out, and_4_out, not_1_out, not_2_out, not_3_out, not_4_out, not_5_out,
       not_6_out, not_7_out, or_1_out, xor_1_out, xor_2_out;

  not not_1 (not_1_out, Bin);
  not not_2 (not_2_out, a1);
  not not_3 (not_3_out, a0);
  not not_4 (not_4_out, b1);
  not not_5 (not_5_out, b0);
  xor xor_1 (xor_1_out, a0, b0);
  not not_6 (not_6_out, xor_1_out);
  xor xor_2 (xor_2_out, b1, a1);
  and and_1 (and_1_out, not_2_out, b1);
  xor xor_3 (out_8, xor_1_out, Bin);
  and and_2 (and_2_out, not_6_out, Bin);
  and and_3 (and_3_out, not_3_out, b0);
  not not_7 (not_7_out, xor_2_out);
  or or_1 (or_1_out, and_2_out, and_3_out);
  xor xor_4 (out_7, or_1_out, xor_2_out);
  and and_4 (and_4_out, or_1_out, not_7_out);
  xor xor_5 (Borrow, and_4_out, and_1_out);
endmodule
