// Logisim project 2.circ as structural Verilog: 1 circuit, main circuit main
module main (
  input  A,
  input  B,
  input  Co,
  input  C,
  input  D,
  output D1,
  output D2,
  output out_8
);

  wire and_1_out, and_2_out, and_3_out, and_4_out, not_1_out, not_2_out, not_3_out, not_4_out, or_1_out,
       xor_1_out, xor_3_out;

  xor xor_1 (xor_1_out, A, B);
  not not_1 (not_1_out, xor_1_out);
  not not_2 (not_2_out, A);
  xor xor_2 (D1, xor_1_out, Co);
  and and_1 (and_1_out, not_1_out, Co);
  and and_2 (and_2_out, not_2_out, B);
  xor xor_3 (xor_3_out, C, D);
  not not_3 (not_3_out, C);
  or or_1 (or_1_out, and_1_out, and_2_out);
  not not_4 (not_4_out, xor_3_out);
  xor xor_4 (D2, or_1_out, xor_3_out);
  and and_3 (and_3_out, or_1_out, not_4_out);
  and and_4 (and_4_out, D, not_3_out);
  or or_2 (out_8, and_3_out, and_4_out);

  // Notes on the sheet:
  //   BORROW
endmodule
