// Logisim project 3.circ as structural Verilog: 1 circuit, main circuit main
module main (
  input  Cin,
  input  [3:0] in_2,
  input  [3:0] in_3,
  output [3:0] out_4,
  output out_5
);

  wire adder_1_cout, adder_2_cout, adder_3_cout;

  Adder #(.width(1)) adder_1 (.a(in_2[0]), .b(in_3[0]), .out(out_4[0]), .cin(Cin), .cout(adder_1_cout));
  Adder #(.width(1)) adder_2 (.a(in_2[1]), .b(in_3[1]), .out(out_4[1]), .cin(adder_1_cout), .cout(adder_2_cout));
  Adder #(.width(1)) adder_3 (.a(in_2[2]), .b(in_3[2]), .out(out_4[2]), .cin(adder_2_cout), .cout(adder_3_cout));
  Adder #(.width(1)) adder_4 (.a(in_2[3]), .b(in_3[3]), .out(out_4[3]), .cin(adder_3_cout), .cout(out_5));

  // Notes on the sheet:
  //   INPUT 1
  //   INPUT 2
  //   SUM
  //   CARRY
endmodule
