// Logisim project 4.circ as structural Verilog: 1 circuit, main circuit main
module main (
  input  Bin,
  input  [3:0] INPUT_1,
  input  [3:0] in_3,
  output [3:0] out_4,
  output out_5
);

  wire subtractor_1_bout, subtractor_2_bout, subtractor_3_bout;

  Subtractor #(.width(1)) subtractor_1 (
    .a(INPUT_1[0]), .b(in_3[0]), .out(out_4[0]), .bin(Bin), .bout(subtractor_1_bout));
  Subtractor #(.width(1)) subtractor_2 (
    .a(INPUT_1[1]), .b(in_3[1]), .out(out_4[1]), .bin(subtractor_1_bout), .bout(subtractor_2_bout));
  Subtractor #(.width(1)) subtractor_3 (
    .a(INPUT_1[2]), .b(in_3[2]), .out(out_4[2]), .bin(subtractor_2_bout), .bout(subtractor_3_bout));
  Subtractor #(.width(1)) subtractor_4 (
    .a(INPUT_1[3]), .b(in_3[3]), .out(out_4[3]), .bin(subtractor_3_bout), .bout(out_5));

  // Notes on the sheet:
  //   INPUT 2
  //   BORROWING
  //   DIFFRENCE
endmodule
