// Logisim project 1bitALU.circ as structural Verilog: 1 circuit, main circuit main
module main (
  input  S1,
  input  S1_2,
  input  A,
  input  B,
  input  C_IN,
  input  [1:0] in_6,
  output C_OUT,
  output RESULT
);

  wire ADD_00_out, AND_01_out, and_1_out, and_2_out, and_3_out, multiplexer_1_out, not_1_out, not_2_out,
       or_1_out, OR_10_out, undriven, undriven_2, undriven_3, undriven_4, xor_1_out;
  wire [1:0] undriven_5;

  and and_1 (and_1_out, B, A);
  xor xor_1 (xor_1_out, B, A);
  and and_2 (and_2_out, B, A);
  or or_1 (or_1_out, B, A);
  Multiplexer #(.select(2)) multiplexer_1 (
    .in0(undriven), .in1(undriven_2), .in2(undriven_3), .in3(undriven_4), .out(multiplexer_1_out),
    .sel(undriven_5));  // open: en
  and and_3 (and_3_out, C_IN, xor_1_out);
  not not_1 (not_1_out, S1);
  or or_2 (C_OUT, and_1_out, and_3_out);
  not not_2 (not_2_out, S1_2);
  and ADD_00 (ADD_00_out, not_2_out, xor_1_out, not_1_out);
  and AND_01 (AND_01_out, S1_2, and_2_out, not_1_out);
  and OR_10 (OR_10_out, S1, or_1_out, not_2_out);
  or or_3 (RESULT, ADD_00_out, AND_01_out, OR_10_out);
endmodule
