// Logisim project CO-asg-5.circ as structural Verilog: 1 circuit, main circuit main
module main (
  input  S1,
  input  S1_2,
  input  A,
  input  B,
  input  B_IN,
  output B_OUT,
  output RESULT
);

  wire and_1_out, and_2_out, and_3_out, NAND_01_out, NOR_10_out, not_1_out, not_2_out, not_3_out, not_4_out,
       not_5_out, not_6_out, or_1_out, SUB_00_out, xor_1_out;

  not not_1 (not_1_out, A);
  and and_1 (and_1_out, B, not_1_out);
  xor xor_1 (xor_1_out, B, A);
  and and_2 (and_2_out, B, A);
  or or_1 (or_1_out, B, A);
  not not_2 (not_2_out, xor_1_out);
  not not_3 (not_3_out, and_2_out);
  not not_4 (not_4_out, or_1_out);
  or or_2 (B_OUT, and_1_out, and_3_out);
  and and_3 (and_3_out, B_IN, not_2_out);
  not not_5 (not_5_out, S1);
  not not_6 (not_6_out, S1_2);
  and SUB_00 (SUB_00_out, not_6_out, xor_1_out, not_5_out);
  and NAND_01 (NAND_01_out, S1_2, not_3_out, not_5_out);
  and NOR_10 (NOR_10_out, S1, not_4_out, not_6_out);
  or or_3 (RESULT, SUB_00_out, NAND_01_out, NOR_10_out);
endmodule
