// Logisim project 1-bit_fullSub.circ as structural Verilog: 1 circuit, main circuit main
module main (
  input  A,
  input  B,
  input  Bin,
  output Diff,
  output Dout
);

  wire and_1_out, and_2_out, not_1_out, not_2_out, not_3_out, not_4_out, xor_1_out;

  not not_1 (not_1_out, A);
  not not_2 (not_2_out, B);
  not not_3 (not_3_out, Bin);
  xor xor_1 (xor_1_out, B, A);
  not not_4 (not_4_out, xor_1_out);
  xor xor_2 (Diff, xor_1_out, Bin);
  and and_1 (and_1_out, B, not_1_out);
  and and_2 (and_2_out, not_4_out, Bin);
  or or_1 (Dout, and_2_out, and_1_out);
endmodule
