// Logisim project 4-bit_Sub.circ as structural Verilog: 1 circuit, main circuit main
module main (
  input  a3,
  input  a2,
  input  a1,
  input  a0,
  input  b3,
  input  b2,
  input  b1,
  input  b0,
  input  Bin,
  output Bout,
  output out_11,
  output out_12,
  output out_13,
  output out_14
);

  wire and_1_out, and_2_out, and_3_out, and_4_out, and_5_out, and_6_out, and_7_out, and_8_out, not_1_out,
       not_2_out, not_3_out, not_4_out, not_5_out, not_6_out, not_7_out, not_8_out, or_1_out, or_2_out,
       or_3_out, xor_1_out, xor_2_out, xor_4_out, xor_5_out;

  not not_1 (not_1_out, a3);
  xor xor_1 (xor_1_out, a0, b0);
  not not_2 (not_2_out, xor_1_out);
  not not_3 (not_3_out, a0);
  not not_4 (not_4_out, a1);
  not not_5 (not_5_out, a2);
  xor xor_2 (xor_2_out, b3, a3);
  and and_1 (and_1_out, b3, not_1_out);
  xor xor_3 (out_14, xor_1_out, Bin);
  and and_2 (and_2_out, Bin, not_2_out);
  and and_3 (and_3_out, not_3_out, b0);
  xor xor_4 (xor_4_out, b1, a1);
  and and_4 (and_4_out, b1, not_4_out);
  xor xor_5 (xor_5_out, b2, a2);
  and and_5 (and_5_out, b2, not_5_out);
  or or_1 (or_1_out, and_2_out, and_3_out);
  not not_6 (not_6_out, xor_4_out);
  xor xor_6 (out_13, or_1_out, xor_4_out);
  and and_6 (and_6_out, or_1_out, not_6_out);
  or or_2 (or_2_out, and_6_out, and_4_out);
  not not_7 (not_7_out, xor_5_out);
  xor xor_7 (out_12, or_2_out, xor_5_out);
  and and_7 (and_7_out, or_2_out, not_7_out);
  or or_3 (or_3_out, and_7_out, and_5_out);
  not not_8 (not_8_out, xor_2_out);
  xor xor_8 (out_11, or_3_out, xor_2_out);
  and and_8 (and_8_out, or_3_out, not_8_out);
  or or_4 (Bout, and_8_out, and_1_out);
endmodule
