// Logisim project 1.circ as structural Verilog: 3 circuits, main circuit main
module main (
  input  [15:0] Address,
  input  in_2,
  input  in_3,
  input  Enable,
  input  [15:0] Data,
  input  To_clear,
  input  To_select,
  input  To_store,
  input  Enable_2,
  input  To_select_2,
  input  [2:0] in_11,
  input  in_12,
  input  in_13,
  input  Enable_3,
  input  [15:0] Data_of_B,
  input  Enable_4,
  input  [2:0] in_17,
  output [15:0] out_18,
  output Cout,
  output Bout,
  output Cout_2,
  output Bout_2
);

  wire Button_2_out, Button_3_out, Button_4_out, Button_5_out, Button_out, Set_to_0_2_out, Set_to_0_3_out,
       Set_to_0_4_out, Set_to_0_out;
  wire [15:0] A_2_q, A_q, B_2_q, B_q, n16_bit_alu_1_result, n16_bit_alu_2_result, ram_1_data;

  Button Button (.out(Button_out));
  RAM #(.addrWidth(16), .dataWidth(16), .bus("separate")) ram_1 (
    .addr(Address), .din(Data), .data(ram_1_data), .sel(To_select), .clk(Button_out), .ld(To_store),
    .clr(To_clear));  // open: str
  Register #(.width(16)) A (.D(ram_1_data), .en(Enable), .Q(A_q), .clk(Button_2_out), .clr(Set_to_0_out));
  Button Set_to_0 (.out(Set_to_0_out));
  Button Button_2 (.out(Button_2_out));
  Register #(.width(16)) B (.D(ram_1_data), .en(Enable_2), .Q(B_q), .clk(Button_3_out), .clr(Set_to_0_2_out));
  Button Set_to_0_2 (.out(Set_to_0_2_out));
  Button Button_3 (.out(Button_3_out));
  Register #(.width(16)) A_2 (.D(ram_1_data), .en(Enable_3), .Q(A_2_q), .clk(Button_4_out), .clr(Set_to_0_3_out));
  Button Set_to_0_3 (.out(Set_to_0_3_out));
  Button Button_4 (.out(Button_4_out));
  Register #(.width(16)) B_2 (.D(Data_of_B), .en(Enable_4), .Q(B_2_q), .clk(Button_5_out), .clr(Set_to_0_4_out));
  Button Set_to_0_4 (.out(Set_to_0_4_out));
  Button Button_5 (.out(Button_5_out));
  _16_bit_ALU u_16_bit_alu_1 (
    .A(A_q), .B(B_q), .Bin(in_2), .Cin(in_3), .Inverse(1'b1), .Operation(in_11),
    .Result(n16_bit_alu_1_result), .Cin_2(Cout), .Bout(Bout));
  _16_bit_ALU u_16_bit_alu_2 (
    .A(A_2_q), .B(B_2_q), .Bin(in_12), .Cin(in_13), .Inverse(1'b1), .Operation(in_17),
    .Result(n16_bit_alu_2_result), .Cin_2(Cout_2), .Bout(Bout_2));
  Multiplexer #(.width(16)) multiplexer_1 (
    .in0(n16_bit_alu_1_result), .in1(n16_bit_alu_2_result), .out(out_18), .sel(To_select_2));  // open: en

  // Notes on the sheet:
  //   RAM
endmodule

module _1_bit_ALU (
  input  Cin,
  input  A,
  input  B,
  input  invert,
  input  Bin,
  input  [2:0] Operation,
  output Cout,
  output result,
  output Bout
);

  wire adder_1_out, multiplexer_1_out, not_1_out, NOT_A_out, NOT_B_out, OR_out, subtractor_1_out;

  not not_1 (not_1_out, B);
  Multiplexer multiplexer_1 (.in0(not_1_out), .in1(B), .out(multiplexer_1_out), .sel(invert));  // open: en
  Adder #(.width(1)) adder_1 (.a(A), .b(multiplexer_1_out), .out(adder_1_out), .cin(Cin), .cout(Cout));
  Subtractor #(.width(1)) subtractor_1 (.a(A), .b(multiplexer_1_out), .out(subtractor_1_out), .bin(Bin), .bout(Bout));
  or OR (OR_out, A, multiplexer_1_out);
  not NOT_A (NOT_A_out, A);
  not NOT_B (NOT_B_out, multiplexer_1_out);
  Multiplexer #(.select(3)) multiplexer_2 (
    .in0(adder_1_out), .in1(subtractor_1_out), .in2(OR_out), .in3(NOT_A_out), .in4(NOT_B_out), .out(result),
    .sel(Operation));  // open: in5, in6, in7, en
endmodule

module _16_bit_ALU (
  input  [15:0] A,
  input  [15:0] B,
  input  Bin,
  input  Cin,
  input  Inverse,
  input  [2:0] Operation,
  output Cin_2,
  output Bout,
  output [15:0] Result
);

  wire n1_bit_alu_1_bout, n1_bit_alu_1_cout, n1_bit_alu_2_bout, n1_bit_alu_2_cout, n1_bit_alu_3_bout,
       n1_bit_alu_3_cout, n1_bit_alu_4_bout, n1_bit_alu_4_cout, n1_bit_alu_5_bout, n1_bit_alu_5_cout,
       n1_bit_alu_6_bout, n1_bit_alu_6_cout, n1_bit_alu_7_bout, n1_bit_alu_7_cout, n1_bit_alu_8_bout,
       n1_bit_alu_8_cout, n1_bit_alu_9_bout, n1_bit_alu_9_cout, n1_bit_alu_10_bout, n1_bit_alu_10_cout,
       n1_bit_alu_11_bout, n1_bit_alu_11_cout, n1_bit_alu_12_bout, n1_bit_alu_12_cout, n1_bit_alu_13_bout,
       n1_bit_alu_13_cout, n1_bit_alu_14_bout, n1_bit_alu_14_cout, n1_bit_alu_15_bout, n1_bit_alu_15_cout;

  _1_bit_ALU u_1_bit_alu_1 (
    .A(A[0]), .B(B[0]), .invert(Inverse), .Cin(Cin), .result(Result[0]), .Cout(n1_bit_alu_1_cout),
    .Operation(Operation), .Bin(Bin), .Bout(n1_bit_alu_1_bout));
  _1_bit_ALU u_1_bit_alu_2 (
    .A(A[1]), .B(B[1]), .invert(Inverse), .Cin(n1_bit_alu_1_cout), .result(Result[1]),
    .Cout(n1_bit_alu_2_cout), .Operation(Operation), .Bin(n1_bit_alu_1_bout), .Bout(n1_bit_alu_2_bout));
  _1_bit_ALU u_1_bit_alu_3 (
    .A(A[2]), .B(B[2]), .invert(Inverse), .Cin(n1_bit_alu_2_cout), .result(Result[2]),
    .Cout(n1_bit_alu_3_cout), .Operation(Operation), .Bin(n1_bit_alu_2_bout), .Bout(n1_bit_alu_3_bout));
  _1_bit_ALU u_1_bit_alu_4 (
    .A(A[3]), .B(B[3]), .invert(Inverse), .Cin(n1_bit_alu_3_cout), .result(Result[3]),
    .Cout(n1_bit_alu_4_cout), .Operation(Operation), .Bin(n1_bit_alu_3_bout), .Bout(n1_bit_alu_4_bout));
  _1_bit_ALU u_1_bit_alu_5 (
    .A(A[4]), .B(B[4]), .invert(Inverse), .Cin(n1_bit_alu_4_cout), .result(Result[4]),
    .Cout(n1_bit_alu_5_cout), .Operation(Operation), .Bin(n1_bit_alu_4_bout), .Bout(n1_bit_alu_5_bout));
  _1_bit_ALU u_1_bit_alu_6 (
    .A(A[5]), .B(B[5]), .invert(Inverse), .Cin(n1_bit_alu_5_cout), .result(Result[5]),
    .Cout(n1_bit_alu_6_cout), .Operation(Operation), .Bin(n1_bit_alu_5_bout), .Bout(n1_bit_alu_6_bout));
  _1_bit_ALU u_1_bit_alu_7 (
    .A(A[6]), .B(B[6]), .invert(Inverse), .Cin(n1_bit_alu_6_cout), .result(Result[6]),
    .Cout(n1_bit_alu_7_cout), .Operation(Operation), .Bin(n1_bit_alu_6_bout), .Bout(n1_bit_alu_7_bout));
  _1_bit_ALU u_1_bit_alu_8 (
    .A(A[7]), .B(B[7]), .invert(Inverse), .Cin(n1_bit_alu_7_cout), .result(Result[7]),
    .Cout(n1_bit_alu_8_cout), .Operation(Operation), .Bin(n1_bit_alu_7_bout), .Bout(n1_bit_alu_8_bout));
  _1_bit_ALU u_1_bit_alu_9 (
    .A(A[8]), .B(B[8]), .invert(Inverse), .Cin(n1_bit_alu_8_cout), .result(Result[8]),
    .Cout(n1_bit_alu_9_cout), .Operation(Operation), .Bin(n1_bit_alu_8_bout), .Bout(n1_bit_alu_9_bout));
  _1_bit_ALU u_1_bit_alu_10 (
    .A(A[9]), .B(B[9]), .invert(Inverse), .Cin(n1_bit_alu_9_cout), .result(Result[9]),
    .Cout(n1_bit_alu_10_cout), .Operation(Operation), .Bin(n1_bit_alu_9_bout), .Bout(n1_bit_alu_10_bout));
  _1_bit_ALU u_1_bit_alu_11 (
    .A(A[10]), .B(B[10]), .invert(Inverse), .Cin(n1_bit_alu_10_cout), .result(Result[10]),
    .Cout(n1_bit_alu_11_cout), .Operation(Operation), .Bin(n1_bit_alu_10_bout), .Bout(n1_bit_alu_11_bout));
  _1_bit_ALU u_1_bit_alu_12 (
    .A(A[11]), .B(B[11]), .invert(Inverse), .Cin(n1_bit_alu_11_cout), .result(Result[11]),
    .Cout(n1_bit_alu_12_cout), .Operation(Operation), .Bin(n1_bit_alu_11_bout), .Bout(n1_bit_alu_12_bout));
  _1_bit_ALU u_1_bit_alu_13 (
    .A(A[12]), .B(B[12]), .invert(Inverse), .Cin(n1_bit_alu_12_cout), .result(Result[12]),
    .Cout(n1_bit_alu_13_cout), .Operation(Operation), .Bin(n1_bit_alu_12_bout), .Bout(n1_bit_alu_13_bout));
  _1_bit_ALU u_1_bit_alu_14 (
    .A(A[13]), .B(B[13]), .invert(Inverse), .Cin(n1_bit_alu_13_cout), .result(Result[13]),
    .Cout(n1_bit_alu_14_cout), .Operation(Operation), .Bin(n1_bit_alu_13_bout), .Bout(n1_bit_alu_14_bout));
  _1_bit_ALU u_1_bit_alu_15 (
    .A(A[14]), .B(B[14]), .invert(Inverse), .Cin(n1_bit_alu_14_cout), .result(Result[14]),
    .Cout(n1_bit_alu_15_cout), .Operation(Operation), .Bin(n1_bit_alu_14_bout), .Bout(n1_bit_alu_15_bout));
  _1_bit_ALU u_1_bit_alu_16 (
    .A(A[15]), .B(B[15]), .invert(Inverse), .Cin(n1_bit_alu_15_cout), .result(Result[15]), .Cout(Cin_2),
    .Operation(Operation), .Bin(n1_bit_alu_15_bout), .Bout(Bout));

  // Other names for the same wires on the sheet: R0 = Result[0]; R1 = Result[1]; R2 = Result[2]; R3 = Result[3];
  //   R4 = Result[4]; R5 = Result[5]; R6 = Result[6]; R7 = Result[7]; R8 = Result[8]; R9 = Result[9];
  //   R10 = Result[10]; R11 = Result[11]; R12 = Result[12]; R13 = Result[13]; R14 = Result[14]; R15 = Result[15]
endmodule
