// Logisim project 1bit_full_adder.circ as structural Verilog: 1 circuit, main circuit main
module main (
  input  x0,
  input  x1,
  input  c_in,
  output s,
  output out_5
);

  wire and_1_out, and_2_out, xor_1_out;

  xor xor_1 (xor_1_out, x0, x1);
  and and_1 (and_1_out, c_in, xor_1_out);
  and and_2 (and_2_out, x0, x1);
  xor xor_2 (s, xor_1_out, c_in);
  or c (out_5, and_1_out, and_2_out);
endmodule
