// Logisim project 1bit_full_subtractor.circ as structural Verilog: 1 circuit, main circuit main
module main (
  input  x0,
  input  x1,
  input  c_in,
  output d,
  output c
);

  wire and_1_out, and_2_out, not_1_out, not_2_out, xor_1_out;

  not not_1 (not_1_out, x0);
  xor xor_1 (xor_1_out, x0, x1);
  and and_1 (and_1_out, not_1_out, x1);
  xor xor_2 (d, xor_1_out, c_in);
  not not_2 (not_2_out, xor_1_out);
  and and_2 (and_2_out, not_2_out, c_in);
  or or_1 (c, and_2_out, and_1_out);
endmodule
