// Logisim project 1bit_half_adder.circ as structural Verilog: 1 circuit, main circuit main
module main (
  input  x0,
  input  x1,
  output s,
  output c
);

  xor xor_1 (s, x0, x1);
  and and_1 (c, x0, x1);
endmodule
