// Logisim project 1bit_half_subtractor.circ as structural Verilog: 1 circuit, main circuit main
module main (
  input  x0,
  input  x1,
  output d,
  output c
);

  wire not_1_out;

  xor xor_1 (d, x0, x1);
  not not_1 (not_1_out, x0);
  and and_1 (c, not_1_out, x1);
endmodule
