// Logisim project 2bit-_full_adder.circ as structural Verilog: 1 circuit, main circuit main
module main (
  input  x0,
  input  x1,
  input  c_in,
  input  x2,
  input  x3,
  output s,
  output s_2,
  output out_8
);

  wire and_1_out, and_2_out, and_3_out, and_4_out, c_out, xor_1_out, xor_2_out;

  xor xor_1 (xor_1_out, x0, x1);
  xor xor_2 (xor_2_out, x2, x3);
  and and_1 (and_1_out, c_in, xor_1_out);
  and and_2 (and_2_out, x0, x1);
  and and_3 (and_3_out, c_out, xor_2_out);
  and and_4 (and_4_out, x2, x3);
  xor xor_3 (s, xor_1_out, c_in);
  or c (c_out, and_1_out, and_2_out);
  xor xor_4 (s_2, xor_2_out, c_out);
  or c_2 (out_8, and_3_out, and_4_out);
endmodule
