// Logisim project 2bit_full_subtractor.circ as structural Verilog: 1 circuit, main circuit main
module main (
  input  x0,
  input  x1,
  input  c_in,
  input  x2,
  input  x3,
  output d,
  output d_2,
  output c
);

  wire and_1_out, and_2_out, and_3_out, and_4_out, not_1_out, not_2_out, not_3_out, not_4_out, or_1_out,
       xor_1_out, xor_2_out;

  not not_1 (not_1_out, x0);
  not not_2 (not_2_out, x2);
  xor xor_1 (xor_1_out, x0, x1);
  and and_1 (and_1_out, not_1_out, x1);
  xor xor_2 (xor_2_out, x2, x3);
  and and_2 (and_2_out, not_2_out, x3);
  not not_3 (not_3_out, xor_1_out);
  not not_4 (not_4_out, xor_2_out);
  xor xor_3 (d, xor_1_out, c_in);
  and and_3 (and_3_out, not_3_out, c_in);
  xor xor_4 (d_2, xor_2_out, or_1_out);
  and and_4 (and_4_out, not_4_out, or_1_out);
  or or_1 (or_1_out, and_3_out, and_1_out);
  or or_2 (c, and_4_out, and_2_out);
endmodule
