// Logisim project 4 3 bit adder.circ as structural Verilog: 2 circuits, main circuit main
module main (
  input  A,
  input  B,
  input  A_2,
  input  B_2,
  input  A_3,
  input  B_3,
  input  A_4,
  input  B_4,
  output SUM,
  output SUM_2,
  output SUM_3,
  output SUM_4,
  output Cout
);

  wire and_1_out, and_2_out, and_3_out, and_4_out, and_5_out, and_6_out, and_7_out, xor_1_out, xor_4_out,
       xor_5_out, xor_7_out, xor_8_out;

  xor xor_1 (xor_1_out, A_3, B_3);
  xor xor_2 (SUM, A, B);
  and and_1 (and_1_out, A, B);
  xor xor_3 (SUM_3, xor_1_out, xor_8_out);
  and and_2 (and_2_out, xor_8_out, xor_1_out);
  and and_3 (and_3_out, B_3, A_3);
  xor xor_4 (xor_4_out, and_2_out, and_3_out);
  xor xor_5 (xor_5_out, A_2, B_2);
  xor xor_6 (SUM_2, xor_5_out, and_1_out);
  and and_4 (and_4_out, and_1_out, xor_5_out);
  and and_5 (and_5_out, B_2, A_2);
  xor xor_7 (xor_7_out, A_4, B_4);
  xor xor_8 (xor_8_out, and_4_out, and_5_out);
  xor xor_9 (SUM_4, xor_7_out, xor_4_out);
  and and_6 (and_6_out, xor_4_out, xor_7_out);
  and and_7 (and_7_out, B_4, A_4);
  xor xor_10 (Cout, and_6_out, and_7_out);

  // Notes on the sheet:
  //   Cin
  //   Cout
  //   Cin
  //   Cout
  //   Cin
  //   Cout
endmodule

module _4add (
  input  in_1,
  input  in_2,
  input  in_3,
  input  in_4,
  input  in_5,
  input  in_6,
  input  in_7,
  input  in_8,
  input  in_9,
  input  in_10,
  input  in_11,
  input  in_12,
  input  in_13,
  input  in_14,
  input  in_15,
  input  in_16,
  output out_17,
  output out_18,
  output out_19,
  output out_20,
  output out_21,
  output out_22,
  output out_23
);

  wire and_2_out, and_3_out, and_4_out, and_5_out, and_6_out, and_7_out, and_8_out, and_9_out, and_10_out,
       and_11_out, and_12_out, main_1_cout, main_1_sum_2, main_1_sum_3, main_1_sum_4, undriven, undriven_2,
       undriven_3;

  and and_1 (out_17, in_1, undriven);
  and and_2 (and_2_out, in_2, undriven);
  and and_3 (and_3_out, in_3, undriven);
  and and_4 (and_4_out, in_4, undriven);
  and and_5 (and_5_out, in_8, undriven_2);
  and and_6 (and_6_out, in_11, undriven_2);
  and and_7 (and_7_out, in_13, undriven_2);
  and and_8 (and_8_out, in_14, undriven_2);
  main main_1 (
    .A(and_2_out), .B(and_3_out), .A_2(and_4_out), .B_2(in_6), .A_3(and_5_out), .B_3(and_6_out),
    .A_4(and_7_out), .B_4(and_8_out), .SUM(out_18), .SUM_2(main_1_sum_2), .SUM_3(main_1_sum_3),
    .SUM_4(main_1_sum_4), .Cout(main_1_cout));
  and and_9 (and_9_out, in_5, undriven_3);
  and and_10 (and_10_out, in_7, undriven_3);
  and and_11 (and_11_out, in_10, undriven_3);
  and and_12 (and_12_out, in_12, undriven_3);
  main main_2 (
    .A(main_1_sum_2), .B(main_1_sum_3), .A_2(main_1_sum_4), .B_2(main_1_cout), .A_3(and_9_out),
    .B_3(and_10_out), .A_4(and_11_out), .B_4(and_12_out), .SUM(out_19), .SUM_2(out_20), .SUM_3(out_21),
    .SUM_4(out_22), .Cout(out_23));
endmodule
