// Logisim project 4X3 multiplier.circ as structural Verilog: 1 circuit, main circuit main
module main (
  input  in_1,
  input  in_2,
  input  in_3,
  input  in_4,
  input  in_5,
  input  in_6,
  input  in_7,
  input  in_8,
  input  in_9,
  input  in_10,
  input  in_11,
  input  in_12,
  input  in_13,
  input  in_14,
  input  in_15,
  input  in_16,
  input  in_17,
  input  in_18,
  output out_19,
  output out_20,
  output out_21,
  output out_22,
  output out_23,
  output out_24,
  output out_25
);

  wire and_2_out, and_3_out, and_4_out, and_5_out, and_6_out, and_7_out, and_8_out, and_9_out, and_10_out,
       and_11_out, and_12_out, undriven, undriven_2, undriven_3;

  and and_1 (out_19, in_1, undriven);
  and and_2 (and_2_out, in_2, undriven);
  and and_3 (and_3_out, in_3, undriven);
  and and_4 (and_4_out, in_5, undriven);
  and and_5 (and_5_out, in_4, undriven_2);
  and and_6 (and_6_out, in_7, undriven_2);
  and and_7 (and_7_out, in_11, undriven_2);
  and and_8 (and_8_out, in_13, undriven_2);
  and and_9 (and_9_out, in_6, undriven_3);
  and and_10 (and_10_out, in_10, undriven_3);
  and and_11 (and_11_out, in_12, undriven_3);
  and and_12 (and_12_out, in_14, undriven_3);
endmodule
