// Logisim project 4bit_full_adder.circ as structural Verilog: 1 circuit, main circuit main
module main (
  input  x0,
  input  x1,
  input  c_in,
  input  x2,
  input  x3,
  input  x0_2,
  input  x1_2,
  input  x2_2,
  input  x3_2,
  output s,
  output s_2,
  output s_3,
  output s_4,
  output out_14
);

  wire and_1_out, and_2_out, and_3_out, and_4_out, and_5_out, and_6_out, and_7_out, and_8_out, c_2_out,
       c_3_out, c_out, xor_1_out, xor_2_out, xor_3_out, xor_4_out;

  xor xor_1 (xor_1_out, x0, x1);
  xor xor_2 (xor_2_out, x2, x3);
  xor xor_3 (xor_3_out, x0_2, x1_2);
  xor xor_4 (xor_4_out, x2_2, x3_2);
  and and_1 (and_1_out, c_2_out, xor_3_out);
  and and_2 (and_2_out, x0_2, x1_2);
  and and_3 (and_3_out, c_3_out, xor_4_out);
  and and_4 (and_4_out, x2_2, x3_2);
  and and_5 (and_5_out, c_in, xor_1_out);
  and and_6 (and_6_out, x0, x1);
  and and_7 (and_7_out, c_out, xor_2_out);
  and and_8 (and_8_out, x2, x3);
  xor xor_5 (s_3, xor_3_out, c_2_out);
  xor xor_6 (s_4, xor_4_out, c_3_out);
  xor xor_7 (s, xor_1_out, c_in);
  or c (c_out, and_5_out, and_6_out);
  xor xor_8 (s_2, xor_2_out, c_out);
  or c_2 (c_2_out, and_7_out, and_8_out);
  or c_3 (c_3_out, and_1_out, and_2_out);
  or c_4 (out_14, and_3_out, and_4_out);
endmodule
