// Logisim project 4bit_full_subtractor.circ as structural Verilog: 1 circuit, main circuit main
module main (
  input  x0,
  input  x1,
  input  c_in,
  input  x2,
  input  x3,
  input  x0_2,
  input  x1_2,
  input  x2_2,
  input  x3_2,
  output d,
  output d_2,
  output d_3,
  output d_4,
  output c
);

  wire and_1_out, and_2_out, and_3_out, and_4_out, and_5_out, and_6_out, and_7_out, and_8_out, not_1_out,
       not_2_out, not_3_out, not_4_out, not_5_out, not_6_out, not_7_out, not_8_out, or_1_out, or_2_out,
       or_3_out, xor_1_out, xor_2_out, xor_3_out, xor_4_out;

  not not_1 (not_1_out, x0);
  not not_2 (not_2_out, x2);
  not not_3 (not_3_out, x0_2);
  not not_4 (not_4_out, x2_2);
  xor xor_1 (xor_1_out, x0, x1);
  and and_1 (and_1_out, not_1_out, x1);
  xor xor_2 (xor_2_out, x2, x3);
  and and_2 (and_2_out, not_2_out, x3);
  xor xor_3 (xor_3_out, x0_2, x1_2);
  and and_3 (and_3_out, not_3_out, x1_2);
  xor xor_4 (xor_4_out, x2_2, x3_2);
  and and_4 (and_4_out, not_4_out, x3_2);
  not not_5 (not_5_out, xor_1_out);
  not not_6 (not_6_out, xor_2_out);
  not not_7 (not_7_out, xor_3_out);
  not not_8 (not_8_out, xor_4_out);
  xor xor_5 (d, xor_1_out, c_in);
  and and_5 (and_5_out, not_5_out, c_in);
  xor xor_6 (d_2, xor_2_out, or_1_out);
  and and_6 (and_6_out, not_6_out, or_1_out);
  xor xor_7 (d_3, xor_3_out, or_2_out);
  and and_7 (and_7_out, not_7_out, or_2_out);
  xor xor_8 (d_4, xor_4_out, or_3_out);
  and and_8 (and_8_out, not_8_out, or_3_out);
  or or_1 (or_1_out, and_5_out, and_1_out);
  or or_2 (or_2_out, and_6_out, and_2_out);
  or or_3 (or_3_out, and_7_out, and_3_out);
  or or_4 (c, and_8_out, and_4_out);
endmodule
