// Logisim project 8bit_ALU.circ as structural Verilog: 1 circuit, main circuit ALU_8bit
module ALU_8bit (
  input  R_type_and_I_type,
  input  clear,
  input  sub,
  input  subI,
  input  [2:0] OP,
  input  [7:0] A,
  input  [7:0] B,
  input  [7:0] address,
  input  write_enable,
  input  [7:0] I_operand,
  output [8:0] out_11
);

  wire adder_1_cout, adder_2_cout, not_1_out, not_2_out, or_1_out, or_4_out, tick_tock_out;
  wire [7:0] adder_1_out, adder_2_out, and_1_out, multiplexer_1_out, multiplexer_2_out, multiplexer_3_out,
       nor_1_out, not_3_out, not_4_out, not_5_out, or_2_out, ram_1_dout, register_1_q, register_2_q,
       xor_1_out;
  wire [8:0] bit_extender_1_out, multiplexer_4_out;
  wire [8:8] or_3_out;

  RAM ram_1 (
    .addr(address), .we(write_enable), .oe(R_type_and_I_type), .clk(tick_tock_out), .din(I_operand),
    .dout(ram_1_dout));
  not not_1 (not_1_out, R_type_and_I_type);
  or or_1 (or_1_out, R_type_and_I_type, not_2_out);
  Clock tick_tock (.out(tick_tock_out));
  not not_2 (not_2_out, R_type_and_I_type);
  Register register_1 (.D(A), .en(or_1_out), .clk(tick_tock_out), .Q(register_1_q), .clr(clear));
  Register register_2 (.D(B), .en(not_1_out), .clk(tick_tock_out), .Q(register_2_q), .clr(clear));
  assign not_3_out = ~register_1_q;  // NOT_Gate not_3, 8 bits wide
  Multiplexer #(.width(8)) multiplexer_1 (.in0(register_2_q), .in1(not_4_out), .out(multiplexer_1_out), .sel(sub));
  assign not_4_out = ~register_2_q;  // NOT_Gate not_4, 8 bits wide
  assign not_5_out = ~ram_1_dout;  // NOT_Gate not_5, 8 bits wide
  Multiplexer #(.width(8)) multiplexer_2 (.in0(ram_1_dout), .in1(not_5_out), .out(multiplexer_2_out), .sel(subI));
  assign and_1_out = register_1_q & multiplexer_1_out;  // AND_Gate and_1, 8 bits wide
  assign or_2_out = register_1_q | multiplexer_1_out;  // OR_Gate or_2, 8 bits wide
  assign xor_1_out = register_1_q ^ multiplexer_1_out;  // XOR_Gate xor_1, 8 bits wide
  assign nor_1_out = ~(register_1_q | multiplexer_1_out);  // NOR_Gate nor_1, 8 bits wide
  Adder adder_1 (.a(register_1_q), .b(multiplexer_1_out), .out(adder_1_out), .cin(sub), .cout(adder_1_cout));
  Adder adder_2 (.a(register_1_q), .b(multiplexer_2_out), .out(adder_2_out), .cin(subI), .cout(adder_2_cout));
  Multiplexer #(.select(3), .width(8)) multiplexer_3 (
    .in0(and_1_out), .in1(or_2_out), .in2(xor_1_out), .in3(nor_1_out), .in4(adder_1_out), .in5(adder_2_out),
    .in6(not_3_out), .in7(not_4_out), .out(multiplexer_3_out), .sel(OP));
  or or_3 (or_3_out[8], adder_1_cout, adder_2_cout);
  assign bit_extender_1_out = {{1{multiplexer_3_out[7]}}, multiplexer_3_out};  // Bit_Extender bit_extender_1
  or or_4 (or_4_out, sub, subI);
  Register #(.width(9)) register_3 (.D(multiplexer_4_out), .clk(tick_tock_out), .Q(out_11), .clr(clear));  // open: en
  Multiplexer #(.width(9)) multiplexer_4 (
    .in0({or_3_out[8], multiplexer_3_out}), .in1(bit_extender_1_out), .out(multiplexer_4_out), .sel(or_4_out));
endmodule
