// Logisim project 8bit_full_adder.circ as structural Verilog: 1 circuit, main circuit main
module main (
  input  x0,
  input  x1,
  input  c_in,
  input  x2,
  input  x3,
  input  x0_2,
  input  x1_2,
  input  x2_2,
  input  x3_2,
  input  x0_3,
  input  x1_3,
  input  x2_3,
  input  x3_3,
  input  x0_4,
  input  x1_4,
  input  x2_4,
  input  x3_4,
  output s,
  output s_2,
  output s_3,
  output s_4,
  output s_5,
  output s_6,
  output s_7,
  output s_8,
  output out_26
);

  wire and_1_out, and_2_out, and_3_out, and_4_out, and_5_out, and_6_out, and_7_out, and_8_out, and_9_out,
       and_10_out, and_11_out, and_12_out, and_13_out, and_14_out, and_15_out, and_16_out, c_2_out, c_3_out,
       c_4_out, c_5_out, c_6_out, c_7_out, c_out, xor_1_out, xor_2_out, xor_3_out, xor_4_out, xor_5_out,
       xor_6_out, xor_7_out, xor_8_out;

  xor xor_1 (xor_1_out, x0_3, x1_3);
  xor xor_2 (xor_2_out, x2_3, x3_3);
  xor xor_3 (xor_3_out, x0_4, x1_4);
  xor xor_4 (xor_4_out, x2_4, x3_4);
  xor xor_5 (xor_5_out, x0, x1);
  xor xor_6 (xor_6_out, x2, x3);
  xor xor_7 (xor_7_out, x0_2, x1_2);
  xor xor_8 (xor_8_out, x2_2, x3_2);
  and and_1 (and_1_out, c_in, xor_5_out);
  and and_2 (and_2_out, x0, x1);
  and and_3 (and_3_out, c_out, xor_6_out);
  and and_4 (and_4_out, x2, x3);
  and and_5 (and_5_out, c_2_out, xor_7_out);
  and and_6 (and_6_out, x0_2, x1_2);
  and and_7 (and_7_out, c_3_out, xor_8_out);
  and and_8 (and_8_out, x2_2, x3_2);
  and and_9 (and_9_out, c_4_out, xor_1_out);
  and and_10 (and_10_out, x0_3, x1_3);
  and and_11 (and_11_out, c_5_out, xor_2_out);
  and and_12 (and_12_out, x2_3, x3_3);
  and and_13 (and_13_out, c_6_out, xor_3_out);
  and and_14 (and_14_out, x0_4, x1_4);
  and and_15 (and_15_out, c_7_out, xor_4_out);
  and and_16 (and_16_out, x2_4, x3_4);
  xor xor_9 (s, xor_5_out, c_in);
  or c (c_out, and_1_out, and_2_out);
  xor xor_10 (s_2, xor_6_out, c_out);
  or c_2 (c_2_out, and_3_out, and_4_out);
  xor xor_11 (s_3, xor_7_out, c_2_out);
  or c_3 (c_3_out, and_5_out, and_6_out);
  xor xor_12 (s_4, xor_8_out, c_3_out);
  or c_4 (c_4_out, and_7_out, and_8_out);
  xor xor_13 (s_5, xor_1_out, c_4_out);
  or c_5 (c_5_out, and_9_out, and_10_out);
  xor xor_14 (s_6, xor_2_out, c_5_out);
  or c_6 (c_6_out, and_11_out, and_12_out);
  xor xor_15 (s_7, xor_3_out, c_6_out);
  or c_7 (c_7_out, and_13_out, and_14_out);
  xor xor_16 (s_8, xor_4_out, c_7_out);
  or c_8 (out_26, and_15_out, and_16_out);
endmodule
