// Logisim project 8bit_full_subtractor.circ as structural Verilog: 1 circuit, main circuit main
module main (
  input  x0,
  input  x1,
  input  c_in,
  input  x2,
  input  x3,
  input  x0_2,
  input  x1_2,
  input  x2_2,
  input  x3_2,
  input  x0_3,
  input  x1_3,
  input  x2_3,
  input  x3_3,
  input  x0_4,
  input  x1_4,
  input  x2_4,
  input  x3_4,
  output d,
  output d_2,
  output d_3,
  output d_4,
  output d_5,
  output d_6,
  output d_7,
  output d_8,
  output c
);

  wire and_1_out, and_2_out, and_3_out, and_4_out, and_5_out, and_6_out, and_7_out, and_8_out, and_9_out,
       and_10_out, and_11_out, and_12_out, and_13_out, and_14_out, and_15_out, and_16_out, not_1_out,
       not_2_out, not_3_out, not_4_out, not_5_out, not_6_out, not_7_out, not_8_out, not_9_out, not_10_out,
       not_11_out, not_12_out, not_13_out, not_14_out, not_15_out, not_16_out, or_1_out, or_2_out, or_3_out,
       or_4_out, or_5_out, or_6_out, or_7_out, xor_1_out, xor_2_out, xor_3_out, xor_4_out, xor_5_out,
       xor_6_out, xor_7_out, xor_8_out;

  xor xor_1 (xor_1_out, x0, x1);
  not not_1 (not_1_out, x0);
  xor xor_2 (xor_2_out, x2, x3);
  not not_2 (not_2_out, x2);
  xor xor_3 (xor_3_out, x0_2, x1_2);
  not not_3 (not_3_out, x0_2);
  xor xor_4 (xor_4_out, x2_2, x3_2);
  not not_4 (not_4_out, x2_2);
  xor xor_5 (xor_5_out, x0_3, x1_3);
  not not_5 (not_5_out, x0_3);
  xor xor_6 (xor_6_out, x2_3, x3_3);
  not not_6 (not_6_out, x2_3);
  xor xor_7 (xor_7_out, x0_4, x1_4);
  not not_7 (not_7_out, x0_4);
  xor xor_8 (xor_8_out, x2_4, x3_4);
  not not_8 (not_8_out, x2_4);
  and and_1 (and_1_out, not_1_out, x1);
  and and_2 (and_2_out, not_2_out, x3);
  and and_3 (and_3_out, not_3_out, x1_2);
  and and_4 (and_4_out, not_4_out, x3_2);
  and and_5 (and_5_out, not_5_out, x1_3);
  and and_6 (and_6_out, not_6_out, x3_3);
  and and_7 (and_7_out, not_7_out, x1_4);
  and and_8 (and_8_out, not_8_out, x3_4);
  xor xor_9 (d, xor_1_out, c_in);
  not not_9 (not_9_out, xor_1_out);
  xor xor_10 (d_2, xor_2_out, or_1_out);
  not not_10 (not_10_out, xor_2_out);
  xor xor_11 (d_3, xor_3_out, or_2_out);
  not not_11 (not_11_out, xor_3_out);
  xor xor_12 (d_4, xor_4_out, or_3_out);
  not not_12 (not_12_out, xor_4_out);
  xor xor_13 (d_5, xor_5_out, or_4_out);
  not not_13 (not_13_out, xor_5_out);
  xor xor_14 (d_6, xor_6_out, or_5_out);
  not not_14 (not_14_out, xor_6_out);
  xor xor_15 (d_7, xor_7_out, or_6_out);
  not not_15 (not_15_out, xor_7_out);
  xor xor_16 (d_8, xor_8_out, or_7_out);
  not not_16 (not_16_out, xor_8_out);
  and and_9 (and_9_out, not_9_out, c_in);
  and and_10 (and_10_out, not_10_out, or_1_out);
  and and_11 (and_11_out, not_11_out, or_2_out);
  and and_12 (and_12_out, not_12_out, or_3_out);
  and and_13 (and_13_out, not_13_out, or_4_out);
  and and_14 (and_14_out, not_14_out, or_5_out);
  and and_15 (and_15_out, not_15_out, or_6_out);
  and and_16 (and_16_out, not_16_out, or_7_out);
  or or_1 (or_1_out, and_9_out, and_1_out);
  or or_2 (or_2_out, and_10_out, and_2_out);
  or or_3 (or_3_out, and_11_out, and_3_out);
  or or_4 (or_4_out, and_12_out, and_4_out);
  or or_5 (or_5_out, and_13_out, and_5_out);
  or or_6 (or_6_out, and_14_out, and_6_out);
  or or_7 (or_7_out, and_15_out, and_7_out);
  or or_8 (c, and_16_out, and_8_out);
endmodule
