// Logisim project A028_CO.circ as structural Verilog: 2 circuits, main circuit main
module main (
  input  [7:0] Address,
  input  [7:0] Data,
  input  To_select,
  input  To_store,
  input  [7:0] in_5,
  input  [7:0] in_6,
  output [7:0] Output
);

  wire binary_to_decimal_1_a_2, binary_to_decimal_1_b_2, binary_to_decimal_1_c_2, binary_to_decimal_1_d_2,
       binary_to_decimal_1_e_2, binary_to_decimal_1_f_2, binary_to_decimal_1_g_2, binary_to_decimal_1_h_2,
       binary_to_decimal_2_a_2, binary_to_decimal_2_b_2, binary_to_decimal_2_c_2, binary_to_decimal_2_d_2,
       binary_to_decimal_2_e_2, binary_to_decimal_2_f_2, binary_to_decimal_2_g_2, binary_to_decimal_2_h_2,
       binary_to_decimal_3_a_2, binary_to_decimal_3_b_2, binary_to_decimal_3_c_2, binary_to_decimal_3_d_2,
       binary_to_decimal_3_e_2, binary_to_decimal_3_f_2, binary_to_decimal_3_g_2, binary_to_decimal_3_h_2,
       Button_out;
  wire [7:0] divider_1_out, divider_1_rem, divider_2_out, divider_2_rem;

  Button Button (.out(Button_out));
  RAM #(.bus("separate")) ram_1 (
    .addr(Address), .din(Data), .data(Output), .sel(To_select), .clk(Button_out), .ld(To_store));  // open: str, clr
  Divider divider_1 (.a(Output), .b(in_5), .out(divider_1_out), .rem(divider_1_rem));  // open: upper
  Divider divider_2 (.a(divider_1_rem), .b(in_6), .out(divider_2_out), .rem(divider_2_rem));  // open: upper
  binary_to_decimal binary_to_decimal_1 (
    .H(divider_1_out[7]), .G(divider_1_out[6]), .F(divider_1_out[5]), .E(divider_1_out[4]),
    .D(divider_1_out[3]), .C(divider_1_out[2]), .B(divider_1_out[1]), .A(divider_1_out[0]),
    .a_2(binary_to_decimal_1_a_2), .b_2(binary_to_decimal_1_b_2), .c_2(binary_to_decimal_1_c_2),
    .d_2(binary_to_decimal_1_d_2), .e_2(binary_to_decimal_1_e_2), .f_2(binary_to_decimal_1_f_2),
    .g_2(binary_to_decimal_1_g_2), .h_2(binary_to_decimal_1_h_2));
  binary_to_decimal binary_to_decimal_2 (
    .H(divider_2_out[7]), .G(divider_2_out[6]), .F(divider_2_out[5]), .E(divider_2_out[4]),
    .D(divider_2_out[3]), .C(divider_2_out[2]), .B(divider_2_out[1]), .A(divider_2_out[0]),
    .a_2(binary_to_decimal_2_a_2), .b_2(binary_to_decimal_2_b_2), .c_2(binary_to_decimal_2_c_2),
    .d_2(binary_to_decimal_2_d_2), .e_2(binary_to_decimal_2_e_2), .f_2(binary_to_decimal_2_f_2),
    .g_2(binary_to_decimal_2_g_2), .h_2(binary_to_decimal_2_h_2));
  binary_to_decimal binary_to_decimal_3 (
    .H(divider_2_rem[7]), .G(divider_2_rem[6]), .F(divider_2_rem[5]), .E(divider_2_rem[4]),
    .D(divider_2_rem[3]), .C(divider_2_rem[2]), .B(divider_2_rem[1]), .A(divider_2_rem[0]),
    .a_2(binary_to_decimal_3_a_2), .b_2(binary_to_decimal_3_b_2), .c_2(binary_to_decimal_3_c_2),
    .d_2(binary_to_decimal_3_d_2), .e_2(binary_to_decimal_3_e_2), .f_2(binary_to_decimal_3_f_2),
    .g_2(binary_to_decimal_3_g_2), .h_2(binary_to_decimal_3_h_2));
  _7_Segment_Display u_7_segment_display_1 (
    .g(binary_to_decimal_1_g_2), .f(binary_to_decimal_1_f_2), .a(binary_to_decimal_1_a_2),
    .b(binary_to_decimal_1_b_2), .e(binary_to_decimal_1_e_2), .d(binary_to_decimal_1_d_2),
    .c(binary_to_decimal_1_c_2), .dp(binary_to_decimal_1_h_2));
  _7_Segment_Display u_7_segment_display_2 (
    .g(binary_to_decimal_2_g_2), .f(binary_to_decimal_2_f_2), .a(binary_to_decimal_2_a_2),
    .b(binary_to_decimal_2_b_2), .e(binary_to_decimal_2_e_2), .d(binary_to_decimal_2_d_2),
    .c(binary_to_decimal_2_c_2), .dp(binary_to_decimal_2_h_2));
  _7_Segment_Display u_7_segment_display_3 (
    .g(binary_to_decimal_3_g_2), .f(binary_to_decimal_3_f_2), .a(binary_to_decimal_3_a_2),
    .b(binary_to_decimal_3_b_2), .e(binary_to_decimal_3_e_2), .d(binary_to_decimal_3_d_2),
    .c(binary_to_decimal_3_c_2), .dp(binary_to_decimal_3_h_2));
endmodule

module binary_to_decimal (
  input  H,
  input  G,
  input  F,
  input  E,
  input  D,
  input  C,
  input  B,
  input  A,
  output a_2,
  output b_2,
  output c_2,
  output d_2,
  output e_2,
  output f_2,
  output g_2,
  output h_2
);

  wire and_1_out, and_2_out, and_3_out, and_4_out, and_5_out, and_6_out, and_7_out, and_8_out, and_9_out,
       and_10_out, and_11_out, and_12_out, and_13_out, and_14_out, and_15_out, and_16_out, not_1_out,
       not_2_out, not_3_out, not_4_out, not_5_out, not_6_out, not_7_out, not_8_out, not_9_out, not_10_out,
       not_11_out, not_12_out, not_13_out, not_14_out, not_15_out, not_16_out, not_17_out, not_18_out,
       not_19_out, not_20_out, not_21_out;

  not not_1 (not_1_out, C);
  and and_1 (and_1_out, not_1_out, not_2_out);
  not not_2 (not_2_out, A);
  and and_2 (and_2_out, C, A);
  not not_3 (not_3_out, C);
  not not_4 (not_4_out, B);
  and and_3 (and_3_out, not_4_out, not_5_out);
  not not_5 (not_5_out, A);
  and and_4 (and_4_out, B, A);
  not not_6 (not_6_out, B);
  or or_1 (c_2, not_6_out, A, C);
  not not_7 (not_7_out, C);
  and and_5 (and_5_out, not_7_out, not_8_out);
  not not_8 (not_8_out, A);
  not not_9 (not_9_out, C);
  and and_6 (and_6_out, not_9_out, B);
  and and_7 (and_7_out, B, not_10_out);
  not not_10 (not_10_out, A);
  not not_11 (not_11_out, B);
  and and_8 (and_8_out, C, not_11_out, A);
  not not_12 (not_12_out, C);
  and and_9 (and_9_out, not_12_out, not_13_out);
  not not_13 (not_13_out, A);
  and and_10 (and_10_out, B, not_14_out);
  not not_14 (not_14_out, A);
  not not_15 (not_15_out, B);
  and and_11 (and_11_out, not_15_out, not_16_out);
  not not_16 (not_16_out, A);
  and and_12 (and_12_out, C, not_17_out);
  not not_17 (not_17_out, B);
  and and_13 (and_13_out, C, not_18_out);
  not not_18 (not_18_out, A);
  not not_19 (not_19_out, C);
  and and_14 (and_14_out, not_19_out, B);
  and and_15 (and_15_out, C, not_20_out);
  not not_20 (not_20_out, B);
  and and_16 (and_16_out, C, not_21_out);
  not not_21 (not_21_out, A);
  or or_2 (a_2, and_1_out, B, and_2_out, D);
  or or_3 (b_2, not_3_out, and_3_out, and_4_out);
  or or_4 (d_2, and_5_out, and_6_out, and_7_out, and_8_out, D);
  or or_5 (e_2, and_9_out, and_10_out);
  or or_6 (f_2, and_11_out, and_12_out, and_13_out, D);
  or or_7 (g_2, and_14_out, and_15_out, and_16_out, D);

  assign h_2 = 1'b1;
endmodule
