// Logisim project A028_CO_Assignment_8_ALU.circ as structural Verilog: 1 circuit, main circuit main
module main (
  input  [15:0] Instructions,
  input  [15:0] Direct_Value,
  input  [15:0] DATA,
  input  [15:0] DATA_2,
  output [15:0] Output,
  output [15:0] Output_2
);

  wire button_1_out, button_2_out, button_3_out, button_4_out, Clock_2_out, Clock_out, not_1_out;
  wire [15:0] A_q, adder_1_out, adder_2_out, B_q, controlled_buffer_1_out, multiplexer_1_out, not_2_out,
       or_1_out, ram_1_data, ram_2_data, subtractor_1_out;

  Button Clock (.out(Clock_out));
  Button Clock_2 (.out(Clock_2_out));
  RAM #(.addrWidth(6), .dataWidth(16), .bus("separate")) ram_1 (
    .addr(Instructions[5:0]), .din(DATA), .data(ram_1_data), .sel(1'b1), .clk(Clock_out), .ld(1'b1));  // open: str, clr
  RAM #(.addrWidth(6), .dataWidth(16), .bus("separate")) ram_2 (
    .addr(Instructions[11:6]), .din(DATA_2), .data(ram_2_data), .sel(1'b1), .clk(Clock_2_out), .ld(1'b1));  // open: str, clr
  Register #(.width(16)) A (.D(ram_1_data), .en(1'b1), .Q(A_q), .clk(button_1_out));  // open: clr
  Button button_1 (.out(button_1_out));
  Register #(.width(16)) B (.D(ram_2_data), .en(1'b1), .Q(B_q), .clk(button_2_out));  // open: clr
  Button button_2 (.out(button_2_out));
  not not_1 (not_1_out, Instructions[15]);
  assign controlled_buffer_1_out = not_1_out ? Direct_Value : 16'bz;  // Controlled_Buffer controlled_buffer_1
  Adder #(.width(16)) adder_1 (.a(A_q), .b(B_q), .out(adder_1_out));  // open: cin, cout
  Subtractor #(.width(16)) subtractor_1 (.a(A_q), .b(B_q), .out(subtractor_1_out));  // open: bin, bout
  assign or_1_out = A_q | B_q;  // OR_Gate or_1, 16 bits wide
  assign not_2_out = ~A_q;  // NOT_Gate not_2, 16 bits wide
  Adder #(.width(16)) adder_2 (.a(A_q), .b(controlled_buffer_1_out), .out(adder_2_out));  // open: cin, cout
  Register #(.width(16)) register_1 (.D(adder_2_out), .en(1'b1), .Q(Output), .clk(button_3_out));  // open: clr
  Button button_3 (.out(button_3_out));
  Multiplexer #(.select(3), .width(16)) multiplexer_1 (
    .in0(adder_1_out), .in1(subtractor_1_out), .in2(or_1_out), .in3(not_2_out), .out(multiplexer_1_out),
    .sel(Instructions[14:12]), .en(Instructions[15]));  // open: in4, in5, in6, in7
  Register #(.width(16)) register_2 (.D(multiplexer_1_out), .en(1'b1), .Q(Output_2), .clk(button_4_out));  // open: clr
  Button button_4 (.out(button_4_out));
endmodule
