// Logisim project A028_CO_U20CS028.circ as structural Verilog: 3 circuits, main circuit main
module main (
  input  [7:0] in_1,
  input  [7:0] in_2,
  output [7:0] Output
);

  wire binarytodecimal_1_a, binarytodecimal_1_b, binarytodecimal_1_c2, binarytodecimal_1_d2,
       binarytodecimal_1_e2, binarytodecimal_1_f2, binarytodecimal_1_g2;
  wire [7:0] multiplier_1_out;

  Multiplier multiplier_1 (.a(in_1), .b(in_2), .out(multiplier_1_out));  // open: cin, cout
  Multiplier multiplier_2 (.a(multiplier_1_out), .b(multiplier_1_out), .out(Output));  // open: cin, cout
  BinaryToDecimal binarytodecimal_1 (
    .h(Output[7]), .g(Output[6]), .f(Output[5]), .e(Output[4]), .d(Output[3]), .c(Output[2]), .b2(Output[1]),
    .a2(Output[0]), .a(binarytodecimal_1_a), .b(binarytodecimal_1_b), .c2(binarytodecimal_1_c2),
    .d2(binarytodecimal_1_d2), .e2(binarytodecimal_1_e2), .f2(binarytodecimal_1_f2), .g2(binarytodecimal_1_g2));
  _7_Segment_Display u_7_segment_display_1 (
    .g(binarytodecimal_1_g2), .f(binarytodecimal_1_f2), .a(binarytodecimal_1_a), .b(binarytodecimal_1_b),
    .e(binarytodecimal_1_e2), .d(binarytodecimal_1_d2), .c(binarytodecimal_1_c2));  // open: dp

  // Notes on the sheet:
  //   x
  //   y
  //   Input lines
  //   A
  //   B
  //   F
  //   G
  //   E
  //   D
  //   C
  //   Dp
  //   output
endmodule

module BinaryToDecimal (
  input  h,
  input  g,
  input  f,
  input  e,
  input  d,
  input  c,
  input  b2,
  input  a2,
  output a,
  output b,
  output c2,
  output d2,
  output e2,
  output f2,
  output g2
);

  wire and_1_out, and_2_out, and_3_out, and_4_out, and_5_out, and_6_out, and_7_out, and_8_out, and_9_out,
       and_10_out, and_11_out, and_12_out, and_13_out, and_14_out, and_15_out, and_16_out, not_1_out,
       not_2_out, not_3_out, not_4_out, not_5_out, not_6_out, not_7_out, not_8_out, not_9_out, not_10_out,
       not_11_out, not_12_out, not_13_out, not_14_out, not_15_out, not_16_out, not_17_out, not_18_out,
       not_19_out, not_20_out, not_21_out;

  not not_1 (not_1_out, c);
  and and_1 (and_1_out, not_1_out, not_2_out);
  not not_2 (not_2_out, a2);
  and and_2 (and_2_out, c, a2);
  not not_3 (not_3_out, c);
  not not_4 (not_4_out, b2);
  and and_3 (and_3_out, not_4_out, not_5_out);
  not not_5 (not_5_out, a2);
  and and_4 (and_4_out, b2, a2);
  not not_6 (not_6_out, b2);
  or or_1 (c2, not_6_out, a2, c);
  not not_7 (not_7_out, c);
  and and_5 (and_5_out, not_7_out, not_8_out);
  not not_8 (not_8_out, a2);
  not not_9 (not_9_out, c);
  and and_6 (and_6_out, not_9_out, b2);
  and and_7 (and_7_out, b2, not_10_out);
  not not_10 (not_10_out, a2);
  not not_11 (not_11_out, b2);
  and and_8 (and_8_out, c, not_11_out, a2);
  not not_12 (not_12_out, c);
  and and_9 (and_9_out, not_12_out, not_13_out);
  not not_13 (not_13_out, a2);
  and and_10 (and_10_out, b2, not_14_out);
  not not_14 (not_14_out, a2);
  not not_15 (not_15_out, b2);
  and and_11 (and_11_out, not_15_out, not_16_out);
  not not_16 (not_16_out, a2);
  and and_12 (and_12_out, c, not_17_out);
  not not_17 (not_17_out, b2);
  and and_13 (and_13_out, c, not_18_out);
  not not_18 (not_18_out, a2);
  not not_19 (not_19_out, c);
  and and_14 (and_14_out, not_19_out, b2);
  and and_15 (and_15_out, c, not_20_out);
  not not_20 (not_20_out, b2);
  and and_16 (and_16_out, c, not_21_out);
  not not_21 (not_21_out, a2);
  or or_2 (a, and_1_out, b2, and_2_out, d);
  or or_3 (b, not_3_out, and_3_out, and_4_out);
  or or_4 (d2, and_5_out, and_6_out, and_7_out, and_8_out, d);
  or or_5 (e2, and_9_out, and_10_out);
  or or_6 (f2, and_11_out, and_12_out, and_13_out, d);
  or or_7 (g2, and_14_out, and_15_out, and_16_out, d);
endmodule

module led (
  input  in_1,
  input  in_2,
  input  in_3,
  input  in_4,
  input  in_5,
  input  in_6,
  input  in_7,
  input  in_8
);

  _7_Segment_Display u_7_segment_display_1 (
    .g(in_3), .f(in_2), .a(in_1), .b(in_4), .e(in_5), .d(in_7), .c(in_8), .dp(in_6));
endmodule
