// Logisim project AA.circ as structural Verilog: 1 circuit, main circuit main
module main (
  input  [7:0] in_1,
  input  [7:0] in_2,
  output [7:0] Output
);

  wire undriven, undriven_2, undriven_3, undriven_4, undriven_5, undriven_6, undriven_7;
  wire [7:0] multiplier_1_out;

  Multiplier multiplier_1 (.a(in_1), .b(in_2), .out(multiplier_1_out));  // open: cin, cout
  Multiplier multiplier_2 (.a(multiplier_1_out), .b(multiplier_1_out), .out(Output));  // open: cin, cout
  _7_Segment_Display u_7_segment_display_1 (
    .g(undriven_6), .f(undriven_7), .a(undriven), .b(undriven_5), .e(undriven_4), .d(undriven_3),
    .c(undriven_2));  // open: dp

  // Notes on the sheet:
  //   Input lines
  //   A
  //   F
  //   G
  //   D
  //   C
  //   E
  //   F
  //   E
  //   B
  //   DP
  //   A
  //   B
  //   G
  //   C
  //   D
  //   Dp
endmodule
