// Logisim project ALU modified.circ as structural Verilog: 1 circuit, main circuit main
module main (
  input  in_1,
  input  [15:0] Instruction,
  input  [7:0] op1_Data,
  input  [7:0] op2_Data,
  output [7:0] output_of_addi,
  output [7:0] output_of_add_sub_not_or
);

  wire button_1_out, button_2_out, button_3_out, button_4_out, not_1_out;
  wire [5:0] controlled_buffer_1_out, controlled_buffer_2_out;
  wire [7:0] adder_1_out, controlled_buffer_3_out, controlled_buffer_4_out, not_2_out, or_1_out, ram_1_data,
       ram_2_data, register_1_q, register_2_q, subtractor_1_out;

  not not_1 (not_1_out, Instruction[15]);
  assign controlled_buffer_1_out = not_1_out ? Instruction[11:6] : 6'bz;  // Controlled_Buffer controlled_buffer_1
  assign controlled_buffer_2_out = not_1_out ? Instruction[5:0] : 6'bz;  // Controlled_Buffer controlled_buffer_2
  Button button_1 (.out(button_1_out));
  Register register_1 (.D(ram_1_data), .en(1'b1), .Q(register_1_q), .clk(button_2_out));  // open: clr
  RAM #(.addrWidth(6), .bus("separate")) ram_1 (
    .addr(controlled_buffer_1_out), .din(op1_Data), .data(ram_1_data), .sel(1'b1), .clk(button_1_out),
    .ld(1'b1));  // open: str, clr
  Button button_2 (.out(button_2_out));
  assign controlled_buffer_3_out = Instruction[15] ? register_1_q : 8'bz;  // Controlled_Buffer controlled_buffer_3
  assign not_2_out = ~register_1_q;  // NOT_Gate not_2, 8 bits wide
  Adder adder_1 (.a(register_1_q), .b(register_2_q), .out(adder_1_out));  // open: cin, cout
  Subtractor subtractor_1 (.a(register_1_q), .b(register_2_q), .out(subtractor_1_out));  // open: bin, bout
  assign or_1_out = register_1_q | register_2_q;  // OR_Gate or_1, 8 bits wide
  assign controlled_buffer_4_out = Instruction[15] ? {{2{in_1}}, Instruction[5:0]} : 8'bz;  // Controlled_Buffer controlled_buffer_4
  Button button_3 (.out(button_3_out));
  RAM #(.addrWidth(6), .bus("separate")) ram_2 (
    .addr(controlled_buffer_2_out), .din(op2_Data), .data(ram_2_data), .sel(1'b1), .clk(button_3_out),
    .ld(1'b1));  // open: str, clr
  Button button_4 (.out(button_4_out));
  Multiplexer #(.select(2), .width(8), .enable("false")) multiplexer_1 (
    .in0(adder_1_out), .in1(subtractor_1_out), .in2(or_1_out), .in3(not_2_out),
    .out(output_of_add_sub_not_or), .sel(Instruction[13:12]));
  Adder adder_2 (.a(controlled_buffer_4_out), .b(controlled_buffer_3_out), .out(output_of_addi));  // open: cin, cout
  Register register_2 (.D(ram_2_data), .en(1'b1), .Q(register_2_q), .clk(button_4_out));  // open: clr

  // Notes on the sheet:
  //   addressing mode
  //   opcode
  //   op1
  //   op2
  //   OPCODE : 
  //   Adder
  //   Subtractor
  //   OR
  //   NOT
  //   x00 --- ADD
  //   x01 --- SUB
  //   x10 --- OR
  //   x11 --- NOT
  //   1XXX --- ADDI
endmodule
