// Logisim project RAM ROM.circ as structural Verilog: 1 circuit, main circuit main
module main (
  input  [7:0] in_1,
  input  [7:0] in_2,
  input  [7:0] in_3,
  input  To_clear,
  input  in_5,
  input  To_store,
  input  in_7,
  input  [7:0] in_8,
  input  [7:0] in_9,
  input  To_clear_2,
  input  in_11,
  input  To_store_2,
  input  in_13,
  input  Set_to_0,
  output [7:0] out_15,
  output [7:0] Output,
  output [7:0] Output_2,
  output [7:0] out_18
);

  wire button_1_out, button_2_out, button_3_out;

  Button button_1 (.out(button_1_out));
  Button button_2 (.out(button_2_out));
  RAM #(.bus("separate")) ram_1 (
    .addr(in_1), .din(in_3), .data(Output), .sel(in_5), .clk(button_1_out), .ld(To_store), .clr(To_clear));  // open: str
  RAM #(.bus("separate")) ram_2 (
    .addr(in_8), .din(in_9), .data(Output_2), .sel(in_11), .clk(button_2_out), .ld(To_store_2),
    .clr(To_clear_2));  // open: str
  Register register_1 (.D(Output_2), .en(in_13), .Q(out_18), .clk(button_3_out), .clr(Set_to_0));
  Button button_3 (.out(button_3_out));
  ROM rom_1 (.addr(in_2), .data(out_15), .sel(in_7));

  // Notes on the sheet:
  //   1
  //   a
  //   c
  //   b
  //   Address
  //   Data
  //   Address
  //   Data
  //   To select
  //   To select
  //   RAM
  //   Button/Clock
  //   RAM
  //   Button/Clock
  //   Enable
  //   Register
  //   Button/Clock
  //   d
  //   D = input
  //   Q = output
  //   en = enable
  //   0 = Set vslue to 0
  //   ROM
  //   contents of rom_1 (hex, n*v repeats v):
  //   0 11 11
endmodule
