// Logisim project U20CS120 LAB ASSIGNMENT.circ as structural Verilog: 3 circuits, main circuit main
module main (
  input  [7:0] in_1,
  input  [7:0] in_2,
  input  in_3,
  input  in_4,
  input  [7:0] in_5,
  input  [7:0] in_6,
  input  in_7,
  input  in_8,
  input  [7:0] in_9,
  input  [7:0] in_10,
  input  in_11,
  input  in_12,
  output [7:0] out_13,
  output [7:0] out_14,
  output [7:0] out_15
);

  wire btod_1_a_2, btod_1_b_2, btod_1_c_2, btod_1_d_2, btod_1_e_2, btod_1_f_2, btod_1_g_2, btod_2_a_2,
       btod_2_b_2, btod_2_c_2, btod_2_d_2, btod_2_e_2, btod_2_f_2, btod_2_g_2, btod_3_a_2, btod_3_b_2,
       btod_3_c_2, btod_3_d_2, btod_3_e_2, btod_3_f_2, btod_3_g_2, clock_1_out, clock_2_out, clock_3_out;

  Clock clock_1 (.out(clock_1_out));
  Clock clock_2 (.out(clock_2_out));
  Clock clock_3 (.out(clock_3_out));
  RAM #(.bus("separate")) ram_1 (
    .addr(in_1), .din(in_2), .data(out_13), .sel(in_3), .clk(clock_1_out), .ld(in_4));  // open: str, clr
  RAM #(.bus("separate")) ram_2 (
    .addr(in_5), .din(in_6), .data(out_14), .sel(in_7), .clk(clock_2_out), .ld(in_8));  // open: str, clr
  RAM #(.bus("separate")) ram_3 (
    .addr(in_9), .din(in_10), .data(out_15), .sel(in_11), .clk(clock_3_out), .ld(in_12));  // open: str, clr
  btod btod_1 (
    .H(out_13[7]), .G(out_13[6]), .F(out_13[5]), .E(out_13[4]), .D(out_13[3]), .C(out_13[2]), .B(out_13[1]),
    .A(out_13[0]), .a_2(btod_1_a_2), .b_2(btod_1_b_2), .c_2(btod_1_c_2), .d_2(btod_1_d_2), .e_2(btod_1_e_2),
    .f_2(btod_1_f_2), .g_2(btod_1_g_2));
  _7_Segment_Display u_7_segment_display_1 (
    .g(btod_1_g_2), .f(btod_1_f_2), .a(btod_1_a_2), .b(btod_1_b_2), .e(btod_1_e_2), .d(btod_1_d_2),
    .c(btod_1_c_2));  // open: dp
  btod btod_2 (
    .H(out_14[7]), .G(out_14[6]), .F(out_14[5]), .E(out_14[4]), .D(out_14[3]), .C(out_14[2]), .B(out_14[1]),
    .A(out_14[0]), .a_2(btod_2_a_2), .b_2(btod_2_b_2), .c_2(btod_2_c_2), .d_2(btod_2_d_2), .e_2(btod_2_e_2),
    .f_2(btod_2_f_2), .g_2(btod_2_g_2));
  btod btod_3 (
    .H(out_15[7]), .G(out_15[6]), .F(out_15[5]), .E(out_15[4]), .D(out_15[3]), .C(out_15[2]), .B(out_15[1]),
    .A(out_15[0]), .a_2(btod_3_a_2), .b_2(btod_3_b_2), .c_2(btod_3_c_2), .d_2(btod_3_d_2), .e_2(btod_3_e_2),
    .f_2(btod_3_f_2), .g_2(btod_3_g_2));
  _7_Segment_Display u_7_segment_display_2 (
    .g(btod_2_g_2), .f(btod_2_f_2), .a(btod_2_a_2), .b(btod_2_b_2), .e(btod_2_e_2), .d(btod_2_d_2),
    .c(btod_2_c_2));  // open: dp
  _7_Segment_Display u_7_segment_display_3 (
    .g(btod_3_g_2), .f(btod_3_f_2), .a(btod_3_a_2), .b(btod_3_b_2), .e(btod_3_e_2), .d(btod_3_d_2),
    .c(btod_3_c_2));  // open: dp

  // Notes on the sheet:
  //   2.
endmodule

module bintodec (
  input  D,
  input  C,
  input  B,
  input  A,
  output a_2,
  output b_2,
  output c_2,
  output d_2,
  output e,
  output f,
  output g
);

  wire and_1_out, and_2_out, and_3_out, and_4_out, and_5_out, and_6_out, and_7_out, and_8_out, and_9_out,
       and_10_out, and_11_out, and_12_out, and_13_out, and_14_out, and_15_out, and_16_out, not_1_out,
       not_2_out, not_3_out, not_4_out, not_5_out, not_6_out, not_7_out, not_8_out, not_9_out, not_10_out,
       not_11_out, not_12_out, not_13_out, not_14_out, not_15_out, not_16_out, not_17_out, not_18_out,
       not_19_out, not_20_out, not_21_out;

  not not_1 (not_1_out, C);
  and and_1 (and_1_out, not_1_out, not_2_out);
  not not_2 (not_2_out, A);
  and and_2 (and_2_out, C, A);
  not not_3 (not_3_out, C);
  not not_4 (not_4_out, B);
  and and_3 (and_3_out, not_4_out, not_5_out);
  not not_5 (not_5_out, A);
  and and_4 (and_4_out, B, A);
  not not_6 (not_6_out, B);
  or or_1 (c_2, not_6_out, A, C);
  not not_7 (not_7_out, C);
  and and_5 (and_5_out, not_7_out, not_8_out);
  not not_8 (not_8_out, A);
  not not_9 (not_9_out, C);
  and and_6 (and_6_out, not_9_out, B);
  and and_7 (and_7_out, B, not_10_out);
  not not_10 (not_10_out, A);
  not not_11 (not_11_out, B);
  and and_8 (and_8_out, C, not_11_out, A);
  not not_12 (not_12_out, C);
  and and_9 (and_9_out, not_12_out, not_13_out);
  not not_13 (not_13_out, A);
  and and_10 (and_10_out, B, not_14_out);
  not not_14 (not_14_out, A);
  not not_15 (not_15_out, B);
  and and_11 (and_11_out, not_15_out, not_16_out);
  not not_16 (not_16_out, A);
  and and_12 (and_12_out, C, not_17_out);
  not not_17 (not_17_out, B);
  and and_13 (and_13_out, C, not_18_out);
  not not_18 (not_18_out, A);
  not not_19 (not_19_out, C);
  and and_14 (and_14_out, not_19_out, B);
  and and_15 (and_15_out, C, not_20_out);
  not not_20 (not_20_out, B);
  and and_16 (and_16_out, C, not_21_out);
  not not_21 (not_21_out, A);
  or or_2 (a_2, and_1_out, B, and_2_out, D);
  or or_3 (b_2, not_3_out, and_3_out, and_4_out);
  or or_4 (d_2, and_5_out, and_6_out, and_7_out, and_8_out, D);
  or or_5 (e, and_9_out, and_10_out);
  or or_6 (f, and_11_out, and_12_out, and_13_out, D);
  or or_7 (g, and_14_out, and_15_out, and_16_out, D);
endmodule

module btod (
  input  H,
  input  G,
  input  F,
  input  E,
  input  D,
  input  C,
  input  B,
  input  A,
  output a_2,
  output b_2,
  output c_2,
  output d_2,
  output e_2,
  output f_2,
  output g_2
);

  wire and_1_out, and_2_out, and_3_out, and_4_out, and_5_out, and_6_out, and_7_out, and_8_out, and_9_out,
       and_10_out, and_11_out, and_12_out, and_13_out, and_14_out, and_15_out, and_16_out, not_1_out,
       not_2_out, not_3_out, not_4_out, not_5_out, not_6_out, not_7_out, not_8_out, not_9_out, not_10_out,
       not_11_out, not_12_out, not_13_out, not_14_out, not_15_out, not_16_out, not_17_out, not_18_out,
       not_19_out, not_20_out, not_21_out;

  not not_1 (not_1_out, C);
  and and_1 (and_1_out, not_1_out, not_2_out);
  not not_2 (not_2_out, A);
  and and_2 (and_2_out, C, A);
  not not_3 (not_3_out, C);
  not not_4 (not_4_out, B);
  and and_3 (and_3_out, not_4_out, not_5_out);
  not not_5 (not_5_out, A);
  and and_4 (and_4_out, B, A);
  not not_6 (not_6_out, B);
  or or_1 (c_2, not_6_out, A, C);
  not not_7 (not_7_out, C);
  and and_5 (and_5_out, not_7_out, not_8_out);
  not not_8 (not_8_out, A);
  not not_9 (not_9_out, C);
  and and_6 (and_6_out, not_9_out, B);
  and and_7 (and_7_out, B, not_10_out);
  not not_10 (not_10_out, A);
  and and_8 (and_8_out, C, not_11_out, A);
  not not_11 (not_11_out, B);
  not not_12 (not_12_out, C);
  and and_9 (and_9_out, not_12_out, not_13_out);
  not not_13 (not_13_out, A);
  and and_10 (and_10_out, B, not_14_out);
  not not_14 (not_14_out, A);
  not not_15 (not_15_out, B);
  and and_11 (and_11_out, not_15_out, not_16_out);
  not not_16 (not_16_out, A);
  and and_12 (and_12_out, C, not_17_out);
  not not_17 (not_17_out, B);
  and and_13 (and_13_out, C, not_18_out);
  not not_18 (not_18_out, A);
  not not_19 (not_19_out, C);
  and and_14 (and_14_out, not_19_out, B);
  and and_15 (and_15_out, C, not_20_out);
  not not_20 (not_20_out, B);
  and and_16 (and_16_out, C, not_21_out);
  not not_21 (not_21_out, A);
  or or_2 (a_2, and_1_out, B, and_2_out, D);
  or or_3 (b_2, not_3_out, and_3_out, and_4_out);
  or or_4 (d_2, and_5_out, and_6_out, and_7_out, and_8_out, D);
  or or_5 (e_2, and_9_out, and_10_out);
  or or_6 (f_2, and_11_out, and_12_out, and_13_out, D);
  or or_7 (g_2, and_14_out, and_15_out, and_16_out, D);
endmodule
