// Logisim project ass4.circ as structural Verilog: 12 circuits, main circuit 1bit half adder
module _1bit_half_adder (
  input  in_1,
  input  in_2,
  output out_3,
  output out_4
);

  xor xor_1 (out_3, in_1, in_2);
  and and_1 (out_4, in_1, in_2);
endmodule

module _1bit_half_subtractor (
  input  in_1,
  input  in_2,
  output out_3,
  output out_4
);

  wire not_1_out;

  not not_1 (not_1_out, in_1);
  xor xor_1 (out_3, in_1, in_2);
  and and_1 (out_4, not_1_out, in_2);
endmodule

module _1bit_full_adder (
  input  in_1,
  input  in_2,
  input  in_3,
  output out_4,
  output out_5
);

  wire and_1_out, and_2_out, xor_1_out;

  xor xor_1 (xor_1_out, in_1, in_2);
  and and_1 (and_1_out, in_1, in_2);
  xor xor_2 (out_4, xor_1_out, in_3);
  and and_2 (and_2_out, xor_1_out, in_3);
  xor xor_3 (out_5, and_2_out, and_1_out);
endmodule

module _1bit_full_subtractot (
  input  in_1,
  input  in_2,
  input  in_3,
  output out_4,
  output out_5
);

  wire and_1_out, and_2_out, not_1_out, not_2_out, xor_1_out;

  not not_1 (not_1_out, in_1);
  xor xor_1 (xor_1_out, in_1, in_2);
  and and_1 (and_1_out, not_1_out, in_2);
  not not_2 (not_2_out, xor_1_out);
  xor xor_2 (out_4, xor_1_out, in_3);
  and and_2 (and_2_out, not_2_out, in_3);
  xor xor_3 (out_5, and_1_out, and_2_out);
endmodule

module _2bit_full_adder (
  input  in_1,
  input  in_2,
  input  in_3,
  input  in_4,
  input  in_5,
  output out_6,
  output out_7,
  output out_8
);

  wire _1bit_full_adder_out_5;

  _1bit_full_adder _1bit_full_adder (
    .in_1(in_1), .in_2(in_2), .in_3(in_3), .out_4(out_6), .out_5(_1bit_full_adder_out_5));
  _1bit_full_adder _1bit_full_adder_2 (
    .in_1(in_4), .in_2(in_5), .in_3(_1bit_full_adder_out_5), .out_4(out_7), .out_5(out_8));
endmodule

module _2bit_full_subtractor (
  input  in_1,
  input  in_2,
  input  in_3,
  input  in_4,
  input  in_5,
  output out_6,
  output out_7,
  output out_8
);

  wire _1bit_full_subtractor_out_5;

  _1bit_full_subtractot _1bit_full_subtractor (
    .in_1(in_1), .in_2(in_2), .in_3(in_3), .out_4(out_6), .out_5(_1bit_full_subtractor_out_5));
  _1bit_full_subtractot _1bit_full_subtractor_2 (
    .in_1(in_4), .in_2(in_5), .in_3(_1bit_full_subtractor_out_5), .out_4(out_7), .out_5(out_8));
endmodule

module _4bit_full_adder (
  input  in_1,
  input  in_2,
  input  in_3,
  input  in_4,
  input  in_5,
  input  in_6,
  input  in_7,
  input  in_8,
  input  in_9,
  output out_10,
  output out_11,
  output out_12,
  output out_13,
  output out_14
);

  wire n2bit_full_adder_1_out_8;

  _2bit_full_adder u_2bit_full_adder_1 (
    .in_1(in_1), .in_2(in_2), .in_3(in_3), .in_4(in_4), .in_5(in_5), .out_6(out_10), .out_7(out_11),
    .out_8(n2bit_full_adder_1_out_8));
  _2bit_full_adder u_2bit_full_adder_2 (
    .in_1(in_6), .in_2(in_7), .in_3(in_8), .in_4(in_9), .in_5(n2bit_full_adder_1_out_8), .out_6(out_12),
    .out_7(out_13), .out_8(out_14));
endmodule

module _4bit_full_subtractor (
  input  in_1,
  input  in_2,
  input  in_3,
  input  in_4,
  input  in_5,
  input  in_6,
  input  in_7,
  input  in_8,
  input  in_9,
  output out_10,
  output out_11,
  output out_12,
  output out_13,
  output out_14
);

  wire n2bit_full_subtractor_1_out_8;

  _2bit_full_subtractor u_2bit_full_subtractor_1 (
    .in_1(in_1), .in_2(in_2), .in_3(in_3), .in_4(in_4), .in_5(in_5), .out_6(out_10), .out_7(out_11),
    .out_8(n2bit_full_subtractor_1_out_8));
  _2bit_full_subtractor u_2bit_full_subtractor_2 (
    .in_1(in_6), .in_2(in_7), .in_3(in_8), .in_4(in_9), .in_5(n2bit_full_subtractor_1_out_8), .out_6(out_12),
    .out_7(out_13), .out_8(out_14));
endmodule

module _8bit_full_adder (
  input  in_1,
  input  in_2,
  input  in_3,
  input  in_4,
  input  in_5,
  input  in_6,
  input  in_7,
  input  in_8,
  input  in_9,
  input  in_10,
  input  in_11,
  input  in_12,
  input  in_13,
  input  in_14,
  input  in_15,
  input  in_16,
  input  in_17,
  output out_18,
  output out_19,
  output out_20,
  output out_21,
  output out_22,
  output out_23,
  output out_24,
  output out_25,
  output out_26
);

  wire n4bit_full_adder_1_out_14;

  _4bit_full_adder u_4bit_full_adder_1 (
    .in_1(in_1), .in_2(in_2), .in_3(in_3), .in_4(in_4), .in_5(in_5), .in_6(in_6), .in_7(in_7), .in_8(in_8),
    .in_9(in_9), .out_10(out_18), .out_11(out_19), .out_12(out_20), .out_13(out_21),
    .out_14(n4bit_full_adder_1_out_14));
  _4bit_full_adder u_4bit_full_adder_2 (
    .in_1(in_10), .in_2(in_11), .in_3(in_12), .in_4(in_13), .in_5(in_14), .in_6(in_15), .in_7(in_16),
    .in_8(in_17), .in_9(n4bit_full_adder_1_out_14), .out_10(out_22), .out_11(out_23), .out_12(out_24),
    .out_13(out_25), .out_14(out_26));
endmodule

module _8bit_full_subtractor (
  input  in_1,
  input  in_2,
  input  in_3,
  input  in_4,
  input  in_5,
  input  in_6,
  input  in_7,
  input  in_8,
  input  in_9,
  input  in_10,
  input  in_11,
  input  in_12,
  input  in_13,
  input  in_14,
  input  in_15,
  input  in_16,
  input  in_17,
  output out_18,
  output out_19,
  output out_20,
  output out_21,
  output out_22,
  output out_23,
  output out_24,
  output out_25,
  output out_26
);

  wire _4bit_full_subtractor_out_14;

  _4bit_full_subtractor _4bit_full_subtractor (
    .in_1(in_1), .in_2(in_2), .in_3(in_3), .in_4(in_4), .in_5(in_5), .in_6(in_6), .in_7(in_7), .in_8(in_8),
    .in_9(in_9), .out_10(out_18), .out_11(out_19), .out_12(out_20), .out_13(out_21),
    .out_14(_4bit_full_subtractor_out_14));
  _4bit_full_subtractor _4bit_full_subtractor_2 (
    .in_1(in_10), .in_2(in_11), .in_3(in_12), .in_4(in_13), .in_5(in_14), .in_6(in_15), .in_7(in_16),
    .in_8(in_17), .in_9(_4bit_full_subtractor_out_14), .out_10(out_22), .out_11(out_23), .out_12(out_24),
    .out_13(out_25), .out_14(out_26));
endmodule

module _16bit_full_adder (
  input  in_1,
  input  in_2,
  input  in_3,
  input  in_4,
  input  in_5,
  input  in_6,
  input  in_7,
  input  in_8,
  input  in_9,
  input  in_10,
  input  in_11,
  input  in_12,
  input  in_13,
  input  in_14,
  input  in_15,
  input  in_16,
  input  in_17,
  input  in_18,
  input  in_19,
  input  in_20,
  input  in_21,
  input  in_22,
  input  in_23,
  input  in_24,
  input  in_25,
  input  in_26,
  input  in_27,
  input  in_28,
  input  in_29,
  input  in_30,
  input  in_31,
  input  in_32,
  input  in_33,
  output out_34,
  output out_35,
  output out_36,
  output out_37,
  output out_38,
  output out_39,
  output out_40,
  output out_41,
  output out_42,
  output out_43,
  output out_44,
  output out_45,
  output out_46,
  output out_47,
  output out_48,
  output out_49
);

  wire n8bit_full_adder_1_out_26, n8bit_full_adder_2_out_20;

  _8bit_full_adder u_8bit_full_adder_1 (
    .in_1(in_1), .in_2(in_2), .in_3(in_3), .in_4(in_4), .in_5(in_5), .in_6(in_6), .in_7(in_7), .in_8(in_8),
    .in_9(in_9), .in_10(in_10), .in_11(in_11), .in_12(in_12), .in_13(in_13), .in_14(in_14), .in_15(in_15),
    .in_16(in_16), .in_17(in_17), .out_18(out_34), .out_19(out_35), .out_20(out_36), .out_21(out_37),
    .out_22(out_38), .out_23(out_39), .out_24(out_40), .out_25(out_41), .out_26(n8bit_full_adder_1_out_26));
  _8bit_full_adder u_8bit_full_adder_2 (
    .in_1(in_18), .in_2(in_19), .in_3(in_20), .in_4(in_21), .in_5(in_22), .in_6(in_23), .in_7(in_24),
    .in_8(in_25), .in_9(in_26), .in_10(in_27), .in_11(in_28), .in_12(in_29), .in_13(in_30), .in_14(in_31),
    .in_15(in_32), .in_16(in_33), .in_17(n8bit_full_adder_1_out_26), .out_18(out_42), .out_19(out_43),
    .out_20(n8bit_full_adder_2_out_20), .out_21(out_44), .out_22(out_45), .out_23(out_46), .out_24(out_47),
    .out_25(out_48), .out_26(out_49));
endmodule

module _16bit_full_subtractor (
  input  in_1,
  input  in_2,
  input  in_3,
  input  in_4,
  input  in_5,
  input  in_6,
  input  in_7,
  input  in_8,
  input  in_9,
  input  in_10,
  input  in_11,
  input  in_12,
  input  in_13,
  input  in_14,
  input  in_15,
  input  in_16,
  input  in_17,
  input  in_18,
  input  in_19,
  input  in_20,
  input  in_21,
  input  in_22,
  input  in_23,
  input  in_24,
  input  in_25,
  input  in_26,
  input  in_27,
  input  in_28,
  input  in_29,
  input  in_30,
  input  in_31,
  input  in_32,
  input  in_33,
  output out_34,
  output out_35,
  output out_36,
  output out_37,
  output out_38,
  output out_39,
  output out_40,
  output out_41,
  output out_42,
  output out_43,
  output out_44,
  output out_45,
  output out_46,
  output out_47,
  output out_48,
  output out_49
);

  wire n8bit_full_subtractor_1_out_26, n8bit_full_subtractor_2_out_20;

  _8bit_full_subtractor u_8bit_full_subtractor_1 (
    .in_1(in_1), .in_2(in_2), .in_3(in_3), .in_4(in_4), .in_5(in_5), .in_6(in_6), .in_7(in_7), .in_8(in_8),
    .in_9(in_9), .in_10(in_10), .in_11(in_11), .in_12(in_12), .in_13(in_13), .in_14(in_14), .in_15(in_15),
    .in_16(in_16), .in_17(in_17), .out_18(out_34), .out_19(out_35), .out_20(out_36), .out_21(out_37),
    .out_22(out_38), .out_23(out_39), .out_24(out_40), .out_25(out_41),
    .out_26(n8bit_full_subtractor_1_out_26));
  _8bit_full_subtractor u_8bit_full_subtractor_2 (
    .in_1(in_18), .in_2(in_19), .in_3(in_20), .in_4(in_21), .in_5(in_22), .in_6(in_23), .in_7(in_24),
    .in_8(in_25), .in_9(in_26), .in_10(in_27), .in_11(in_28), .in_12(in_29), .in_13(in_30), .in_14(in_31),
    .in_15(in_32), .in_16(in_33), .in_17(n8bit_full_subtractor_1_out_26), .out_18(out_42), .out_19(out_43),
    .out_20(n8bit_full_subtractor_2_out_20), .out_21(out_44), .out_22(out_45), .out_23(out_46),
    .out_24(out_47), .out_25(out_48), .out_26(out_49));
endmodule
