// Logisim project practical-5.circ as structural Verilog
module _1bit_full_adder (
  input  Xo,
  input  X1,
  input  C_in,
  output S,
  output C
);

  wire and_1_out, and_2_out, xor_1_out;

  xor xor_1 (xor_1_out, Xo, X1);
  and and_1 (and_1_out, Xo, X1);
  xor xor_2 (S, xor_1_out, C_in);
  and and_2 (and_2_out, xor_1_out, C_in);
  or or_1 (C, and_2_out, and_1_out);
endmodule

module _1bit_full_subtracor (
  input  X0,
  input  X1,
  input  C_in_Borrow,
  output D_difference,
  output C_Borrow
);

  wire and_1_out, and_2_out, not_1_out, not_2_out, xor_1_out;

  not not_1 (not_1_out, X0);
  xor xor_1 (xor_1_out, X0, X1);
  and and_1 (and_1_out, not_1_out, X1);
  not not_2 (not_2_out, xor_1_out);
  xor xor_2 (D_difference, xor_1_out, C_in_Borrow);
  and and_2 (and_2_out, not_2_out, C_in_Borrow);
  or or_1 (C_Borrow, and_1_out, and_2_out);
endmodule

module _1bit_half_adder (
  input  X0,
  input  X1,
  output S,
  output C
);

  xor xor_1 (S, X0, X1);
  and and_1 (C, X0, X1);
endmodule

module _1bit_half_subtractor (
  input  X0,
  input  X1,
  output D,
  output C_Borrow
);

  wire not_1_out;

  not not_1 (not_1_out, X0);
  xor xor_1 (D, X0, X1);
  and and_1 (C_Borrow, not_1_out, X1);
endmodule

module _2bit_full_adder (
  input  Xo,
  input  Yo,
  input  C_in,
  input  X1,
  input  Y1,
  output S0,
  output S1,
  output C_out
);

  wire _1bit_full_adder_c;

  _1bit_full_adder _1bit_full_adder (.Xo(Xo), .X1(Yo), .C_in(C_in), .S(S0), .C(_1bit_full_adder_c));
  _1bit_full_adder _1_bit_full_adder (.Xo(X1), .X1(Y1), .C_in(_1bit_full_adder_c), .S(S1), .C(C_out));
endmodule

module _2_bit_full_subtractor (
  input  X0,
  input  Y0,
  input  C_in_Borrow,
  input  X1,
  input  Y1,
  output D0,
  output D1,
  output C_out_Borrow
);

  wire _1_bit_full_subtractor_c_borrow;

  _1bit_full_subtracor _1_bit_full_subtractor (
    .X0(X0), .X1(Y0), .C_in_Borrow(C_in_Borrow), .D_difference(D0), .C_Borrow(_1_bit_full_subtractor_c_borrow));
  _1bit_full_subtracor _1_bit_full_subtractor_2 (
    .X0(X1), .X1(Y1), .C_in_Borrow(_1_bit_full_subtractor_c_borrow), .D_difference(D1),
    .C_Borrow(C_out_Borrow));
endmodule

module _4_bit_full_adder (
  input  X0,
  input  Y0,
  input  C_in,
  input  X1,
  input  Y1,
  input  X2,
  input  Y2,
  input  X3,
  input  Y3,
  output So,
  output S1,
  output S2,
  output S3,
  output C_out
);

  wire _1_bit_full_adder_2_c, _1_bit_full_adder_3_c, _1_bit_full_adder_c;

  _1bit_full_adder _1_bit_full_adder (.Xo(X0), .X1(Y0), .C_in(C_in), .S(So), .C(_1_bit_full_adder_c));
  _1bit_full_adder _1_bit_full_adder_2 (
    .Xo(X1), .X1(Y1), .C_in(_1_bit_full_adder_c), .S(S1), .C(_1_bit_full_adder_2_c));
  _1bit_full_adder _1_bit_full_adder_3 (
    .Xo(X2), .X1(Y2), .C_in(_1_bit_full_adder_2_c), .S(S2), .C(_1_bit_full_adder_3_c));
  _1bit_full_adder _1_bit_full_adder_4 (.Xo(X3), .X1(Y3), .C_in(_1_bit_full_adder_3_c), .S(S3), .C(C_out));
endmodule

module _4_bit_full_subtractor (
  input  X0,
  input  Y0,
  input  C_in_Borrow,
  input  X1,
  input  Y1,
  input  X2,
  input  Y2,
  input  X3,
  input  Y3,
  output D0,
  output D1,
  output D2,
  output D3,
  output C_out_Borrow
);

  wire _1_bit_full_subtractor_2_c_borrow, _1_bit_full_subtractor_3_c_borrow, _1_bit_full_subtractor_c_borrow;

  _1bit_full_subtracor _1_bit_full_subtractor (
    .X0(X0), .X1(Y0), .C_in_Borrow(C_in_Borrow), .D_difference(D0), .C_Borrow(_1_bit_full_subtractor_c_borrow));
  _1bit_full_subtracor _1_bit_full_subtractor_2 (
    .X0(X1), .X1(Y1), .C_in_Borrow(_1_bit_full_subtractor_c_borrow), .D_difference(D1),
    .C_Borrow(_1_bit_full_subtractor_2_c_borrow));
  _1bit_full_subtracor _1_bit_full_subtractor_3 (
    .X0(X2), .X1(Y2), .C_in_Borrow(_1_bit_full_subtractor_2_c_borrow), .D_difference(D2),
    .C_Borrow(_1_bit_full_subtractor_3_c_borrow));
  _1bit_full_subtracor _1_bit_full_subtractor_4 (
    .X0(X3), .X1(Y3), .C_in_Borrow(_1_bit_full_subtractor_3_c_borrow), .D_difference(D3),
    .C_Borrow(C_out_Borrow));
endmodule

module _4_3_array_multiplier (
  input  in_1,
  input  in_2,
  input  in_3,
  input  in_4,
  input  in_5,
  input  in_6,
  input  in_7,
  input  in_8,
  input  in_9,
  input  in_10,
  input  in_11,
  output out_12,
  output out_13,
  output out_14,
  output out_15,
  output out_16,
  output out_17
);

  wire and_1_out, and_2_out, and_3_out, and_4_out, and_5_out, and_6_out, and_7_out, and_8_out, and_9_out,
       and_10_out, and_11_out, n4_bit_full_adder_2_s1, n4_bit_full_adder_2_s2, n4_bit_full_adder_2_s3,
       n4_bit_full_adder_2_so;

  and and_1 (and_1_out, in_1, in_9);
  and and_2 (and_2_out, in_1, in_6);
  and and_3 (and_3_out, in_2, in_9);
  and and_4 (and_4_out, in_1, in_5);
  and and_5 (and_5_out, in_2, in_6);
  and and_6 (and_6_out, in_3, in_9);
  _4_bit_full_adder u_4_bit_full_adder_1 (
    .X0(and_9_out), .Y0(n4_bit_full_adder_2_s1), .C_in(in_10), .X1(and_6_out), .Y1(n4_bit_full_adder_2_s2),
    .X2(and_3_out), .Y2(n4_bit_full_adder_2_s3), .X3(and_1_out), .Y3(in_11), .So(out_13), .S1(out_17),
    .S2(out_16), .S3(out_15), .C_out(out_14));
  and and_7 (and_7_out, in_2, in_5);
  and and_8 (and_8_out, in_3, in_6);
  _4_bit_full_adder u_4_bit_full_adder_2 (
    .X0(and_11_out), .Y0(and_10_out), .C_in(in_7), .X1(and_8_out), .Y1(and_7_out), .X2(and_5_out),
    .Y2(and_4_out), .X3(and_2_out), .Y3(in_8), .So(n4_bit_full_adder_2_so), .S1(n4_bit_full_adder_2_s1),
    .S2(n4_bit_full_adder_2_s2), .S3(n4_bit_full_adder_2_s3));  // open: C_out
  and and_9 (and_9_out, in_4, in_9);
  and and_10 (and_10_out, in_3, in_5);
  and and_11 (and_11_out, in_4, in_6);
  and and_12 (out_12, in_4, in_5);
endmodule
