// Logisim project practical-7.circ as structural Verilog: 4 circuits, main circuit 8-bit-RAM
module _8_bit_RAM (
  input  [7:0] Address,
  input  [7:0] Address_2,
  input  [7:0] Data,
  input  select,
  input  store,
  input  select_2,
  input  [7:0] Address_3,
  input  [7:0] Data_2,
  input  select_3,
  input  store_2,
  input  Enable,
  output [7:0] Output,
  output [7:0] Output_2,
  output [7:0] Output_3,
  output [7:0] Output_4
);

  wire CLK_2_out, CLK_3_out, CLK_out, CLR_2_out, CLR_3_out, CLR_out;

  Button CLK (.out(CLK_out));
  Button CLK_2 (.out(CLK_2_out));
  RAM #(.bus("separate")) ram_1 (
    .addr(Address), .din(Data), .data(Output), .sel(select), .clk(CLK_out), .ld(store), .clr(CLR_out));  // open: str
  Button CLR (.out(CLR_out));
  RAM #(.bus("separate")) ram_2 (
    .addr(Address_3), .din(Data_2), .data(Output_3), .sel(select_3), .clk(CLK_2_out), .ld(store_2),
    .clr(CLR_2_out));  // open: str
  Button CLR_2 (.out(CLR_2_out));
  Register Register (.D(Output_3), .en(Enable), .Q(Output_4), .clk(CLK_3_out), .clr(CLR_3_out));
  Button CLK_3 (.out(CLK_3_out));
  Button CLR_3 (.out(CLR_3_out));
  ROM rom_1 (.addr(Address_2), .data(Output_2), .sel(select_2));

  // Notes on the sheet:
  //   Q1 A,B
  //   Q1 C
  //   Q2
endmodule

module binary_7segment_led (
  input  h,
  input  g,
  input  f,
  input  e,
  input  d,
  input  c,
  input  b,
  input  a,
  output a_2,
  output b_2,
  output c_2,
  output d_2,
  output e_2,
  output f_2,
  output g_2
);

  wire and_1_out, and_2_out, and_3_out, and_4_out, and_5_out, and_6_out, and_7_out, and_8_out, and_9_out,
       and_10_out, and_11_out, and_12_out, and_13_out, and_14_out, not_1_out, not_2_out, not_3_out,
       not_4_out, not_5_out, not_6_out, not_7_out, not_8_out, not_9_out, not_10_out, not_11_out, not_12_out,
       not_13_out, not_14_out, not_15_out, not_16_out, not_17_out, not_18_out, not_19_out;

  not not_1 (not_1_out, c);
  and and_1 (and_1_out, not_1_out, not_2_out);
  not not_2 (not_2_out, a);
  and and_2 (and_2_out, c, a);
  not not_3 (not_3_out, c);
  not not_4 (not_4_out, b);
  and and_3 (and_3_out, not_4_out, not_5_out);
  not not_5 (not_5_out, a);
  and and_4 (and_4_out, b, a);
  not not_6 (not_6_out, b);
  or or_1 (c_2, not_6_out, a, c);
  not not_7 (not_7_out, a);
  not not_8 (not_8_out, c);
  and and_5 (and_5_out, not_8_out, b);
  and and_6 (and_6_out, c, not_9_out);
  not not_9 (not_9_out, b);
  not not_10 (not_10_out, c);
  and and_7 (and_7_out, not_10_out, not_11_out);
  not not_11 (not_11_out, a);
  and and_8 (and_8_out, b, not_12_out);
  not not_12 (not_12_out, a);
  not not_13 (not_13_out, b);
  and and_9 (and_9_out, not_13_out, not_14_out);
  not not_14 (not_14_out, a);
  and and_10 (and_10_out, c, not_15_out);
  not not_15 (not_15_out, b);
  and and_11 (and_11_out, c, not_16_out);
  not not_16 (not_16_out, a);
  not not_17 (not_17_out, c);
  and and_12 (and_12_out, not_17_out, b);
  and and_13 (and_13_out, c, not_18_out);
  not not_18 (not_18_out, b);
  and and_14 (and_14_out, c, not_19_out);
  not not_19 (not_19_out, a);
  or or_2 (a_2, and_1_out, b, and_2_out, d);
  or or_3 (b_2, not_3_out, and_3_out, and_4_out);
  or or_4 (d_2, not_7_out, and_5_out, and_6_out, d);
  or or_5 (e_2, and_7_out, and_8_out);
  or or_6 (f_2, and_9_out, and_10_out, and_11_out, d);
  or or_7 (g_2, and_12_out, and_13_out, and_14_out, d);
endmodule

module binary_to_7seg_led (
  input  [7:0] Address,
  input  [7:0] Data,
  input  select,
  input  store,
  input  [7:0] Address_2,
  input  [7:0] Address_3,
  input  [7:0] Address_4,
  output [7:0] Output
);

  wire binary_7segment_led_1_a_2, binary_7segment_led_1_b_2, binary_7segment_led_1_c_2,
       binary_7segment_led_1_d_2, binary_7segment_led_1_e_2, binary_7segment_led_1_f_2,
       binary_7segment_led_1_g_2, binary_7segment_led_2_a_2, binary_7segment_led_2_b_2,
       binary_7segment_led_2_c_2, binary_7segment_led_2_d_2, binary_7segment_led_2_e_2,
       binary_7segment_led_2_f_2, binary_7segment_led_2_g_2, binary_7segment_led_3_a_2,
       binary_7segment_led_3_b_2, binary_7segment_led_3_c_2, binary_7segment_led_3_d_2,
       binary_7segment_led_3_e_2, binary_7segment_led_3_f_2, binary_7segment_led_3_g_2, CLK_out, CLR_out;
  wire [7:0] divider_1_out, divider_2_out, divider_2_rem, divider_3_rem;

  RAM #(.bus("separate")) ram_1 (
    .addr(Address), .din(Data), .data(Output), .sel(select), .clk(CLK_out), .ld(store), .clr(CLR_out));  // open: str
  Button CLK (.out(CLK_out));
  Button CLR (.out(CLR_out));
  Divider divider_1 (.a(divider_2_rem), .b(Address_4), .out(divider_1_out));  // open: upper, rem
  Divider divider_2 (.a(Output), .b(Address_2), .out(divider_2_out), .rem(divider_2_rem));  // open: upper
  Divider divider_3 (.a(divider_2_rem), .b(Address_3), .rem(divider_3_rem));  // open: out, upper
  binary_7segment_led binary_7segment_led_1 (
    .h(divider_3_rem[7]), .g(divider_3_rem[6]), .f(divider_3_rem[5]), .e(divider_3_rem[4]),
    .d(divider_3_rem[3]), .c(divider_3_rem[2]), .b(divider_3_rem[1]), .a(divider_3_rem[0]),
    .a_2(binary_7segment_led_1_a_2), .b_2(binary_7segment_led_1_b_2), .c_2(binary_7segment_led_1_c_2),
    .d_2(binary_7segment_led_1_d_2), .e_2(binary_7segment_led_1_e_2), .f_2(binary_7segment_led_1_f_2),
    .g_2(binary_7segment_led_1_g_2));
  binary_7segment_led binary_7segment_led_2 (
    .h(divider_1_out[7]), .g(divider_1_out[6]), .f(divider_1_out[5]), .e(divider_1_out[4]),
    .d(divider_1_out[3]), .c(divider_1_out[2]), .b(divider_1_out[1]), .a(divider_1_out[0]),
    .a_2(binary_7segment_led_2_a_2), .b_2(binary_7segment_led_2_b_2), .c_2(binary_7segment_led_2_c_2),
    .d_2(binary_7segment_led_2_d_2), .e_2(binary_7segment_led_2_e_2), .f_2(binary_7segment_led_2_f_2),
    .g_2(binary_7segment_led_2_g_2));
  binary_7segment_led binary_7segment_led_3 (
    .h(divider_2_out[7]), .g(divider_2_out[6]), .f(divider_2_out[5]), .e(divider_2_out[4]),
    .d(divider_2_out[3]), .c(divider_2_out[2]), .b(divider_2_out[1]), .a(divider_2_out[0]),
    .a_2(binary_7segment_led_3_a_2), .b_2(binary_7segment_led_3_b_2), .c_2(binary_7segment_led_3_c_2),
    .d_2(binary_7segment_led_3_d_2), .e_2(binary_7segment_led_3_e_2), .f_2(binary_7segment_led_3_f_2),
    .g_2(binary_7segment_led_3_g_2));
  _7_Segment_Display u_7_segment_display_1 (
    .g(binary_7segment_led_1_g_2), .f(binary_7segment_led_1_f_2), .a(binary_7segment_led_1_a_2),
    .b(binary_7segment_led_1_b_2), .e(binary_7segment_led_1_e_2), .d(binary_7segment_led_1_d_2),
    .c(binary_7segment_led_1_c_2));  // open: dp
  _7_Segment_Display u_7_segment_display_2 (
    .g(binary_7segment_led_2_g_2), .f(binary_7segment_led_2_f_2), .a(binary_7segment_led_2_a_2),
    .b(binary_7segment_led_2_b_2), .e(binary_7segment_led_2_e_2), .d(binary_7segment_led_2_d_2),
    .c(binary_7segment_led_2_c_2));  // open: dp
  _7_Segment_Display u_7_segment_display_3 (
    .g(binary_7segment_led_3_g_2), .f(binary_7segment_led_3_f_2), .a(binary_7segment_led_3_a_2),
    .b(binary_7segment_led_3_b_2), .e(binary_7segment_led_3_e_2), .d(binary_7segment_led_3_d_2),
    .c(binary_7segment_led_3_c_2));  // open: dp

  // Notes on the sheet:
  //   Q3
endmodule

module _4bit_decoder (
  input  d,
  input  c,
  input  b,
  input  a,
  output a_2,
  output b_2,
  output c_2,
  output d_2,
  output e,
  output f,
  output g
);

  wire and_1_out, and_2_out, and_3_out, and_4_out, and_5_out, and_6_out, and_7_out, and_8_out, and_9_out,
       and_10_out, and_11_out, and_12_out, and_13_out, and_14_out, and_15_out, and_16_out, not_1_out,
       not_2_out, not_3_out, not_4_out, not_5_out, not_6_out, not_7_out, not_8_out, not_9_out, not_10_out,
       not_11_out, not_12_out, not_13_out, not_14_out, not_15_out, not_16_out, not_17_out, not_18_out,
       not_19_out, not_20_out, not_21_out;

  not not_1 (not_1_out, c);
  and and_1 (and_1_out, not_1_out, not_2_out);
  not not_2 (not_2_out, a);
  and and_2 (and_2_out, c, a);
  not not_3 (not_3_out, c);
  not not_4 (not_4_out, b);
  and and_3 (and_3_out, not_4_out, not_5_out);
  not not_5 (not_5_out, a);
  and and_4 (and_4_out, b, a);
  not not_6 (not_6_out, b);
  or or_1 (c_2, not_6_out, a, c);
  not not_7 (not_7_out, c);
  and and_5 (and_5_out, not_7_out, not_8_out);
  not not_8 (not_8_out, a);
  not not_9 (not_9_out, c);
  and and_6 (and_6_out, not_9_out, b);
  and and_7 (and_7_out, b, not_10_out);
  not not_10 (not_10_out, a);
  and and_8 (and_8_out, c, not_11_out, a);
  not not_11 (not_11_out, b);
  not not_12 (not_12_out, c);
  and and_9 (and_9_out, not_12_out, not_13_out);
  not not_13 (not_13_out, a);
  and and_10 (and_10_out, b, not_14_out);
  not not_14 (not_14_out, a);
  not not_15 (not_15_out, b);
  and and_11 (and_11_out, not_15_out, not_16_out);
  not not_16 (not_16_out, a);
  and and_12 (and_12_out, c, not_17_out);
  not not_17 (not_17_out, b);
  and and_13 (and_13_out, c, not_18_out);
  not not_18 (not_18_out, a);
  not not_19 (not_19_out, c);
  and and_14 (and_14_out, not_19_out, b);
  and and_15 (and_15_out, c, not_20_out);
  not not_20 (not_20_out, b);
  and and_16 (and_16_out, c, not_21_out);
  not not_21 (not_21_out, a);
  or or_2 (a_2, and_1_out, b, and_2_out, d);
  or or_3 (b_2, not_3_out, and_3_out, and_4_out);
  or or_4 (d_2, and_5_out, and_6_out, and_7_out, and_8_out, d);
  or or_5 (e, and_9_out, and_10_out);
  or or_6 (f, and_11_out, and_12_out, and_13_out, d);
  or or_7 (g, and_14_out, and_15_out, and_16_out, d);
endmodule
