// Logisim project 2nd.circ as structural Verilog: 2 circuits, main circuit 1st_streetlight
module _1st_streetlight (
  input  in_1,
  input  in_2
);

  wire and_1_out, and_2_out, clock_1_out, not_1_out, or_1_out;

  not not_1 (not_1_out, in_2);
  and and_1 (and_1_out, 1'b1, clock_1_out);
  Clock #(.highDuration(2)) clock_1 (.out(clock_1_out));
  and and_2 (and_2_out, in_1, not_1_out);
  or or_1 (or_1_out, and_1_out, and_2_out);
  LED led_1 (.in(or_1_out));
endmodule

module _2nd (
  input  [7:0] in_1,
  input  [2:0] in_2,
  input  [2:0] in_3,
  input  [2:0] in_4,
  input  [2:0] in_5,
  input  [2:0] in_6,
  input  [2:0] in_7,
  output [5:0] out_8
);

  Multiplexer #(.select(3)) multiplexer_1 (
    .in0(in_1[0]), .in1(in_1[1]), .in2(in_1[2]), .in3(in_1[3]), .in4(in_1[4]), .in5(in_1[5]), .in6(in_1[6]),
    .in7(in_1[7]), .out(out_8[5]), .sel(in_2));  // open: en
  Multiplexer #(.select(3)) multiplexer_2 (
    .in0(in_1[0]), .in1(in_1[1]), .in2(in_1[2]), .in3(in_1[3]), .in4(in_1[4]), .in5(in_1[5]), .in6(in_1[6]),
    .in7(in_1[7]), .out(out_8[4]), .sel(in_3));  // open: en
  Multiplexer #(.select(3)) multiplexer_3 (
    .in0(in_1[0]), .in1(in_1[1]), .in2(in_1[2]), .in3(in_1[3]), .in4(in_1[4]), .in5(in_1[5]), .in6(in_1[6]),
    .in7(in_1[7]), .out(out_8[3]), .sel(in_4));  // open: en
  Multiplexer #(.select(3)) multiplexer_4 (
    .in0(in_1[0]), .in1(in_1[1]), .in2(in_1[2]), .in3(in_1[3]), .in4(in_1[4]), .in5(in_1[5]), .in6(in_1[6]),
    .in7(in_1[7]), .out(out_8[2]), .sel(in_5));  // open: en
  Multiplexer #(.select(3)) multiplexer_5 (
    .in0(in_1[0]), .in1(in_1[1]), .in2(in_1[2]), .in3(in_1[3]), .in4(in_1[4]), .in5(in_1[5]), .in6(in_1[6]),
    .in7(in_1[7]), .out(out_8[1]), .sel(in_6));  // open: en
  Multiplexer #(.select(3)) multiplexer_6 (
    .in0(in_1[0]), .in1(in_1[1]), .in2(in_1[2]), .in3(in_1[3]), .in4(in_1[4]), .in5(in_1[5]), .in6(in_1[6]),
    .in7(in_1[7]), .out(out_8[0]), .sel(in_7));  // open: en
endmodule
