// Logisim project practical.circ as structural Verilog: 1 circuit, main circuit main
module main (
  input  [7:0] in_1,
  output [5:0] out_2
);


  assign out_2 = {in_1[0], in_1[1], in_1[2], in_1[5], in_1[6], in_1[7]};
endmodule
